// Logisim project Contador de 5 a 28.circ as structural Verilog: 1 circuit, main circuit main
module main (
  input  E,
  output Q0,
  output Q1,
  output Q2,
  output Q3,
  output Q4
);

  wire and_1_out, CLK_out, t_ff_2_qn;

  Clock CLK (.out(CLK_out));
  T_Flip_Flop #(.trigger("falling")) t_ff_1 (.clk(CLK_out), .T(E), .Q(Q0), .preset(and_1_out));  // open: Qn, reset, en
  and and_1 (and_1_out, Q0, t_ff_2_qn, Q2, Q3, Q4);
  T_Flip_Flop #(.trigger("falling")) t_ff_2 (
    .clk(Q0), .T(E), .Q(Q1), .Qn(t_ff_2_qn), .reset(and_1_out));  // open: preset, en
  T_Flip_Flop #(.trigger("falling")) t_ff_3 (.clk(Q1), .T(E), .Q(Q2), .preset(and_1_out));  // open: Qn, reset, en
  T_Flip_Flop #(.trigger("falling")) t_ff_4 (.clk(Q2), .T(E), .Q(Q3), .reset(and_1_out));  // open: Qn, preset, en
  T_Flip_Flop #(.trigger("falling")) t_ff_5 (.clk(Q3), .T(E), .Q(Q4), .reset(and_1_out));  // open: Qn, preset, en
endmodule
