// Logisim project Contador gerador de uma sequencia aleatoria.circ as structural Verilog: 2 circuits, main circuit main
module main (
  input  Q2,
  input  Q1,
  input  Q0,
  output J2,
  output K2,
  output J1,
  output K1,
  output J0,
  output K0
);

  wire not_1_out, not_2_out, not_3_out, not_4_out;

  or or_1 (K2, Q0, Q1);
  not not_1 (not_1_out, Q2);
  not not_2 (not_2_out, Q0);
  not not_3 (not_3_out, Q2);
  not not_4 (not_4_out, Q1);
  or or_2 (J1, not_1_out, not_2_out, Q1);
  or or_3 (J0, not_3_out, not_4_out);

  assign J2 = Q1;
  assign K0 = 1'b1;
  assign K1 = 1'b1;
endmodule

module Contador_Gerador_de_uma_Sequencia_Qualquer (
  output Q2,
  output Q1,
  output Q0
);

  wire clock_1_out, j_k_ff_1_qn, j_k_ff_2_qn, j_k_ff_3_qn, or_1_out, or_2_out, or_3_out, or_4_out;

  Clock clock_1 (.out(clock_1_out));
  or or_1 (or_1_out, Q2, Q1);
  or or_2 (or_2_out, Q1, Q0);
  J_K_Flip_Flop j_k_ff_1 (
    .J(or_1_out), .clk(clock_1_out), .K(or_2_out), .Q(Q2), .Qn(j_k_ff_1_qn));  // open: preset, en, reset
  or or_3 (or_3_out, Q1, j_k_ff_3_qn, j_k_ff_1_qn);
  J_K_Flip_Flop j_k_ff_2 (
    .J(or_3_out), .clk(clock_1_out), .K(1'b1), .Q(Q1), .Qn(j_k_ff_2_qn));  // open: preset, en, reset
  or or_4 (or_4_out, j_k_ff_1_qn, j_k_ff_2_qn);
  J_K_Flip_Flop j_k_ff_3 (
    .J(or_4_out), .clk(clock_1_out), .K(1'b1), .Q(Q0), .Qn(j_k_ff_3_qn));  // open: preset, en, reset
endmodule
