// Logisim project Contador impar - 1 a A.circ as structural Verilog
module Contandor_Par (
  input  CLK,
  input  CLR,
  output Q3,
  output Q2,
  output Q1,
  output Q0
);

  wire auxiliar_1_j0, auxiliar_1_j1, auxiliar_1_j2, auxiliar_1_j3, auxiliar_1_k0, auxiliar_1_k1,
       auxiliar_1_k2, auxiliar_1_k3;

  J_K_Flip_Flop j_k_ff_1 (
    .J(auxiliar_1_j3), .clk(CLK), .K(auxiliar_1_k3), .Q(Q3), .reset(CLR));  // open: Qn, preset, en
  J_K_Flip_Flop j_k_ff_2 (
    .J(auxiliar_1_j2), .clk(CLK), .K(auxiliar_1_k2), .Q(Q2), .reset(CLR));  // open: Qn, preset, en
  J_K_Flip_Flop j_k_ff_3 (
    .J(auxiliar_1_j1), .clk(CLK), .K(auxiliar_1_k1), .Q(Q1), .reset(CLR));  // open: Qn, preset, en
  J_K_Flip_Flop j_k_ff_4 (
    .J(auxiliar_1_j0), .clk(CLK), .K(auxiliar_1_k0), .Q(Q0), .reset(CLR));  // open: Qn, preset, en
  Auxiliar auxiliar_1 (
    .J3(auxiliar_1_j3), .K3(auxiliar_1_k3), .J2(auxiliar_1_j2), .K2(auxiliar_1_k2), .J1(auxiliar_1_j1),
    .K1(auxiliar_1_k1), .J0(auxiliar_1_j0), .K0(auxiliar_1_k0), .Q3(Q3), .Q2(Q2), .Q1(Q1), .Q0(Q0));
endmodule

module Auxiliar (
  input  Q3,
  input  Q2,
  input  Q1,
  input  Q0,
  output J3,
  output K3,
  output J2,
  output K2,
  output J1,
  output K1,
  output J0,
  output K0
);

  and and_1 (J3, Q1, Q2);
  and and_2 (J2, Q1, ~Q3);  // AND_Gate
  and and_3 (K0, Q1, Q3);

  assign J0 = Q0;
  assign J1 = 1'b1;
  assign K1 = 1'b1;
  assign K2 = Q1;
  assign K3 = Q1;
endmodule

module Main (
  input  CLR
);

  wire clock_1_out, contandor_par_1_q0, contandor_par_1_q1, contandor_par_1_q2, contandor_par_1_q3;

  Clock clock_1 (.out(clock_1_out));
  Contandor_Par contandor_par_1 (
    .CLK(clock_1_out), .CLR(CLR), .Q3(contandor_par_1_q3), .Q2(contandor_par_1_q2), .Q1(contandor_par_1_q1),
    .Q0(contandor_par_1_q0));
  _7_Segment_Display u_7_segment_display_1 ();  // open: g, f, a, b, e, d, c, dp
endmodule
