// Logisim project Contador impar.circ as structural Verilog: 4 circuits, main circuit contador impar
module contador_impar (
  input  rt
);

  wire clock_1_out, cont_1_q0, cont_1_q1, cont_1_q2, cont_1_q3, decodificador_1_b1, decodificador_1_b2,
       decodificador_1_b3, decodificador_1_c1, decodificador_1_c2, decodificador_1_c3, decodificador_1_c4;

  Clock clock_1 (.out(clock_1_out));
  decodificador decodificador_1 (
    .Q3(cont_1_q3), .Q2(cont_1_q2), .Q1(cont_1_q1), .Q0(cont_1_q0), .c1(decodificador_1_c1),
    .c2(decodificador_1_c2), .c3(decodificador_1_c3), .c4(decodificador_1_c4), .b1(decodificador_1_b1),
    .b2(decodificador_1_b2), .b3(decodificador_1_b3));
  cont cont_1 (.c(clock_1_out), .r(rt), .Q3(cont_1_q3), .Q2(cont_1_q2), .Q1(cont_1_q1), .Q0(cont_1_q0));
  _7_Segment_Display u_7_segment_display_1 (
    .g(decodificador_1_c1), .f(decodificador_1_c2), .a(decodificador_1_c3), .b(decodificador_1_c4),
    .e(decodificador_1_b1), .d(decodificador_1_b2), .c(decodificador_1_b3));  // open: dp
endmodule

module x (
  input  Q2,
  input  Q1,
  input  Q3,
  output out_4,
  output out_5,
  output out_6,
  output out_7,
  output out_8,
  output out_9,
  output out_10,
  output out_11
);

  wire not_1_out;

  not not_1 (not_1_out, Q3);
  and and_1 (out_4, Q2, Q1);
  and and_2 (out_6, not_1_out, Q1);
  not not_2 (out_10, 1'b1);

  assign out_5 = Q1;
  assign out_7 = Q1;
  assign out_8 = 1'b1;
  assign out_9 = 1'b1;
  assign out_11 = out_10;
endmodule

module cont (
  input  c,
  input  r,
  output Q3,
  output Q2,
  output Q1,
  output Q0
);

  wire j_k_ff_4_qn, or_1_out, x_1_out_4, x_1_out_5, x_1_out_6, x_1_out_7, x_1_out_8, x_1_out_9, x_1_out_10,
       x_1_out_11;

  or or_1 (or_1_out, r, j_k_ff_4_qn);
  x x_1 (
    .Q3(Q3), .Q2(Q2), .Q1(Q1), .out_4(x_1_out_4), .out_5(x_1_out_5), .out_6(x_1_out_6), .out_7(x_1_out_7),
    .out_8(x_1_out_8), .out_9(x_1_out_9), .out_10(x_1_out_10), .out_11(x_1_out_11));
  J_K_Flip_Flop j_k_ff_1 (.J(x_1_out_4), .clk(c), .K(x_1_out_5), .Q(Q3), .reset(or_1_out));  // open: Qn, preset, en
  J_K_Flip_Flop j_k_ff_2 (.J(x_1_out_6), .clk(c), .K(x_1_out_7), .Q(Q2), .preset(or_1_out));  // open: Qn, en, reset
  J_K_Flip_Flop j_k_ff_3 (.J(x_1_out_8), .clk(c), .K(x_1_out_9), .Q(Q1), .reset(or_1_out));  // open: Qn, preset, en
  J_K_Flip_Flop j_k_ff_4 (
    .J(x_1_out_10), .clk(c), .K(x_1_out_11), .Q(Q0), .Qn(j_k_ff_4_qn), .preset(or_1_out));  // open: en, reset
endmodule

module decodificador (
  input  Q3,
  input  Q2,
  input  Q1,
  input  Q0,
  output c1,
  output c2,
  output c3,
  output c4,
  output b1,
  output b2,
  output b3
);

  wire and_1_out, and_2_out, and_3_out, and_4_out, and_5_out, and_6_out, and_7_out, and_8_out, and_9_out,
       and_10_out, and_11_out, and_12_out, and_13_out, and_14_out, and_15_out, and_16_out, and_17_out,
       and_18_out, and_19_out, and_20_out, and_21_out, and_22_out, and_23_out, and_24_out, and_25_out,
       and_26_out, and_27_out, and_28_out, and_29_out, and_30_out, and_31_out, and_32_out, and_33_out,
       and_34_out, and_35_out, not_1_out, not_2_out, not_3_out, not_4_out, not_5_out, not_6_out, not_7_out,
       not_8_out, not_9_out, not_10_out, not_11_out, not_12_out, not_13_out, not_14_out, not_15_out,
       not_16_out, not_17_out, not_18_out, not_19_out, not_20_out, not_21_out, not_22_out, not_23_out,
       not_24_out, not_25_out, not_26_out, not_27_out, not_28_out, not_29_out, not_30_out, not_31_out,
       not_32_out, not_33_out, not_34_out, not_35_out, not_36_out, not_37_out, not_38_out, not_39_out,
       not_40_out, not_41_out, not_42_out, not_43_out;

  not not_1 (not_1_out, Q2);
  and and_1 (and_1_out, not_1_out, Q1);
  and and_2 (and_2_out, Q1, not_2_out);
  not not_2 (not_2_out, Q0);
  not not_3 (not_3_out, Q3);
  and and_3 (and_3_out, not_3_out, Q2, not_4_out);
  not not_4 (not_4_out, Q1);
  and and_4 (and_4_out, Q3, not_5_out);
  not not_5 (not_5_out, Q2);
  and and_5 (and_5_out, Q3, Q0);
  not not_6 (not_6_out, Q1);
  and and_6 (and_6_out, not_6_out, not_7_out);
  not not_7 (not_7_out, Q0);
  not not_8 (not_8_out, Q3);
  and and_7 (and_7_out, not_8_out, Q2, not_9_out);
  not not_9 (not_9_out, Q1);
  and and_8 (and_8_out, Q2, not_10_out);
  not not_10 (not_10_out, Q0);
  and and_9 (and_9_out, Q3, not_11_out);
  not not_11 (not_11_out, Q2);
  and and_10 (and_10_out, Q3, Q1);
  not not_12 (not_12_out, Q2);
  and and_11 (and_11_out, not_12_out, not_13_out);
  not not_13 (not_13_out, Q0);
  not not_14 (not_14_out, Q3);
  and and_12 (and_12_out, not_14_out, Q1);
  not not_15 (not_15_out, Q3);
  and and_13 (and_13_out, not_15_out, Q2, Q0);
  and and_14 (and_14_out, Q2, Q1);
  and and_15 (and_15_out, Q3, not_16_out, not_17_out);
  not not_16 (not_16_out, Q2);
  not not_17 (not_17_out, Q1);
  and and_16 (and_16_out, Q3, not_18_out);
  not not_18 (not_18_out, Q0);
  not not_19 (not_19_out, Q3);
  and and_17 (and_17_out, not_19_out, not_20_out);
  not not_20 (not_20_out, Q2);
  not not_21 (not_21_out, Q3);
  not not_22 (not_22_out, Q1);
  and and_18 (and_18_out, not_21_out, not_22_out, not_23_out);
  not not_23 (not_23_out, Q0);
  not not_24 (not_24_out, Q2);
  and and_19 (and_19_out, not_24_out, not_25_out);
  not not_25 (not_25_out, Q0);
  not not_26 (not_26_out, Q3);
  and and_20 (and_20_out, not_26_out, Q1, Q0);
  not not_27 (not_27_out, Q1);
  and and_21 (and_21_out, Q3, not_27_out, Q0);
  not not_28 (not_28_out, Q2);
  and and_22 (and_22_out, not_28_out, not_29_out);
  not not_29 (not_29_out, Q0);
  and and_23 (and_23_out, Q1, not_30_out);
  not not_30 (not_30_out, Q0);
  and and_24 (and_24_out, Q3, Q1);
  and and_25 (and_25_out, Q3, Q2);
  not not_31 (not_31_out, Q3);
  and and_26 (and_26_out, not_31_out, not_32_out, not_33_out);
  not not_32 (not_32_out, Q2);
  not not_33 (not_33_out, Q0);
  not not_34 (not_34_out, Q2);
  and and_27 (and_27_out, not_34_out, Q1, Q0);
  and and_28 (and_28_out, Q2, not_35_out, Q0);
  not not_35 (not_35_out, Q1);
  and and_29 (and_29_out, Q2, Q1, not_36_out);
  not not_36 (not_36_out, Q0);
  and and_30 (and_30_out, Q3, not_37_out);
  not not_37 (not_37_out, Q1);
  not not_38 (not_38_out, Q3);
  and and_31 (and_31_out, not_38_out, not_39_out);
  not not_39 (not_39_out, Q1);
  not not_40 (not_40_out, Q3);
  and and_32 (and_32_out, not_40_out, Q0);
  not not_41 (not_41_out, Q1);
  and and_33 (and_33_out, not_41_out, Q0);
  not not_42 (not_42_out, Q3);
  and and_34 (and_34_out, not_42_out, Q2);
  and and_35 (and_35_out, Q3, not_43_out);
  not not_43 (not_43_out, Q2);
  or or_1 (c1, and_1_out, and_2_out, and_3_out, and_4_out, and_5_out);
  or or_2 (c2, and_6_out, and_7_out, and_8_out, and_9_out, and_10_out);
  or or_3 (c4, and_17_out, and_18_out, and_19_out, and_20_out, and_21_out);
  or or_4 (b1, and_22_out, and_23_out, and_24_out, and_25_out);
  or or_5 (b2, and_26_out, and_27_out, and_28_out, and_29_out, and_30_out);
  or or_6 (b3, and_31_out, and_32_out, and_33_out, and_34_out, and_35_out);
  or or_7 (c3, and_11_out, and_12_out, and_13_out, and_14_out, and_15_out, and_16_out);
endmodule
