// Logisim project Numeros primos.circ as structural Verilog: 4 circuits, main circuit main
module main (
  input  in_1
);

  wire clock_1_out, contador_1_q0, contador_1_q1, contador_1_q2, decodificador_1_a, decodificador_1_b,
       decodificador_1_c, decodificador_1_d, decodificador_1_e, decodificador_1_f, decodificador_1_g;

  Clock clock_1 (.out(clock_1_out));
  Contador contador_1 (.CLK(clock_1_out), .CLR(in_1), .Q2(contador_1_q2), .Q1(contador_1_q1), .Q0(contador_1_q0));
  Decodificador decodificador_1 (
    .Q0(contador_1_q2), .Q1(contador_1_q1), .Q2(contador_1_q0), .a(decodificador_1_a), .b(decodificador_1_b),
    .c(decodificador_1_c), .d(decodificador_1_d), .e(decodificador_1_e), .f(decodificador_1_f),
    .g(decodificador_1_g));
  _7_Segment_Display u_7_segment_display_1 (
    .g(decodificador_1_g), .f(decodificador_1_f), .a(decodificador_1_a), .b(decodificador_1_b),
    .e(decodificador_1_e), .d(decodificador_1_d), .c(decodificador_1_c));  // open: dp
endmodule

module Decodificador (
  input  Q0,
  input  Q1,
  input  Q2,
  output a,
  output b,
  output c,
  output d,
  output e,
  output f,
  output g
);

  wire and_1_out, and_2_out, and_3_out, and_4_out, and_5_out, and_6_out, and_7_out, and_8_out, and_9_out,
       and_10_out, and_11_out, and_12_out, and_13_out, and_14_out, and_15_out, and_16_out, not_1_out,
       not_2_out, not_3_out, not_4_out, not_5_out, not_6_out, not_7_out, not_8_out, not_9_out, not_10_out,
       not_11_out, not_12_out, not_13_out, not_14_out, not_15_out, not_16_out, not_17_out, not_18_out,
       not_19_out, not_20_out, not_21_out;

  not not_1 (not_1_out, Q0);
  not not_2 (not_2_out, Q2);
  not not_3 (not_3_out, Q1);
  not not_4 (not_4_out, Q2);
  not not_5 (not_5_out, Q1);
  not not_6 (not_6_out, Q0);
  not not_7 (not_7_out, Q2);
  not not_8 (not_8_out, Q0);
  not not_9 (not_9_out, Q2);
  not not_10 (not_10_out, Q1);
  not not_11 (not_11_out, Q0);
  not not_12 (not_12_out, Q2);
  not not_13 (not_13_out, Q2);
  not not_14 (not_14_out, Q1);
  not not_15 (not_15_out, Q2);
  not not_16 (not_16_out, Q1);
  not not_17 (not_17_out, Q2);
  not not_18 (not_18_out, Q0);
  not not_19 (not_19_out, Q1);
  not not_20 (not_20_out, Q2);
  and and_1 (and_1_out, not_1_out, not_2_out);
  and and_2 (and_2_out, Q0, Q2);
  not not_21 (not_21_out, Q0);
  and and_3 (and_3_out, not_3_out, not_4_out);
  and and_4 (and_4_out, Q1, Q2);
  or or_1 (c, not_5_out, Q2, Q0);
  and and_5 (and_5_out, not_6_out, not_7_out);
  and and_6 (and_6_out, not_8_out, Q1);
  and and_7 (and_7_out, Q1, not_9_out);
  and and_8 (and_8_out, Q0, not_10_out, Q2);
  and and_9 (and_9_out, not_11_out, not_12_out);
  and and_10 (and_10_out, Q1, not_13_out);
  and and_11 (and_11_out, not_14_out, not_15_out);
  and and_12 (and_12_out, Q0, not_16_out);
  and and_13 (and_13_out, Q0, not_17_out);
  and and_14 (and_14_out, not_18_out, Q1);
  and and_15 (and_15_out, Q0, not_19_out);
  and and_16 (and_16_out, Q0, not_20_out);
  or or_2 (a, and_1_out, Q1, and_2_out);
  or or_3 (b, not_21_out, and_3_out, and_4_out);
  or or_4 (d, and_5_out, and_6_out, and_7_out, and_8_out);
  or or_5 (e, and_9_out, and_10_out);
  or or_6 (f, and_11_out, and_12_out, and_13_out);
  or or_7 (g, and_14_out, and_15_out, and_16_out);
endmodule

module Contador (
  input  CLK,
  input  CLR,
  output Q2,
  output Q1,
  output Q0
);

  wire aux_1_j0, aux_1_j1, aux_1_j2, aux_1_k0, aux_1_k1, aux_1_k2;

  J_K_Flip_Flop j_k_ff_1 (.J(aux_1_j2), .clk(CLK), .K(aux_1_k2), .Q(Q2), .reset(CLR));  // open: Qn, preset, en
  J_K_Flip_Flop j_k_ff_2 (.J(aux_1_j1), .clk(CLK), .K(aux_1_k1), .Q(Q1), .reset(CLR));  // open: Qn, preset, en
  J_K_Flip_Flop j_k_ff_3 (.J(aux_1_j0), .clk(CLK), .K(aux_1_k0), .Q(Q0), .reset(CLR));  // open: Qn, preset, en
  Aux aux_1 (
    .Q2(Q2), .Q1(Q1), .Q0(Q0), .J2(aux_1_j2), .K2(aux_1_k2), .J1(aux_1_j1), .K1(aux_1_k1), .J0(aux_1_j0),
    .K0(aux_1_k0));
endmodule

module Aux (
  input  Q2,
  input  Q1,
  input  Q0,
  output J2,
  output K2,
  output J1,
  output K1,
  output J0,
  output K0
);

  wire and_1_out, and_2_out;

  and and_1 (and_1_out, ~Q0, ~Q1, ~Q2);  // AND_Gate
  and and_2 (and_2_out, Q0, Q1, ~Q2);  // AND_Gate
  and and_3 (K2, Q2, Q1);
  and and_4 (K0, Q0, ~Q1, ~Q2);  // AND_Gate
  or or_1 (J2, and_1_out, and_2_out);
  or or_2 (J1, Q2, Q0);
  or or_3 (K1, Q2, Q0);

  assign J0 = Q1;
endmodule
