// Logisim project Somador binário.circ as structural Verilog: 6 circuits, main circuit main
module main (
  input  _1___Negativo,
  input  in_2,
  input  in_3,
  input  in_4,
  input  in_5,
  input  in_6,
  input  in_7,
  input  in_8,
  input  in_9,
  output S7,
  output S6,
  output S5,
  output S4,
  output S3,
  output S2,
  output S1,
  output S0,
  output Resto
);

  wire auxiliar_1_f1, button_1_out;
  wire [3:0] auxiliar_1_out_3, auxiliar_1_out_4, auxiliar_1_out_5, \botão_1_out_2 ;
  wire [7:0] entrada_1_w, entrada_1_x, entrada_1_y, multiplexer_1_out, negator_1_out;

  Button button_1 (.out(button_1_out));
  Multiplexer #(.width(8)) multiplexer_1 (
    .in0({in_2, in_3, in_4, in_5, in_6, in_7, in_8, in_9}), .in1(negator_1_out), .out(multiplexer_1_out),
    .sel(_1___Negativo));  // open: en
  Negator negator_1 (.in({in_2, in_3, in_4, in_5, in_6, in_7, in_8, in_9}), .out(negator_1_out));
  \Botão  \botão_1  (.in_1(button_1_out), .out_2(\botão_1_out_2 ));
  Entrada entrada_1 (
    .in_1(multiplexer_1_out), .X(entrada_1_x), .Y(entrada_1_y), .W(entrada_1_w), .in_2(\botão_1_out_2 ));
  Somador somador_1 (
    .X(entrada_1_x), .W(entrada_1_w), .Y(entrada_1_y), .Soma({S7, S6, S5, S4, S3, S2, S1, S0}), .Resto(Resto));
  _7_Segment_Display u_7_segment_display_1 (.g(auxiliar_1_f1));  // open: f, a, b, e, d, c, dp
  Auxiliar auxiliar_1 (
    .in_1({S7, S6, S5, S4, S3, S2, S1, S0}), .F1(auxiliar_1_f1), .out_3(auxiliar_1_out_3),
    .out_4(auxiliar_1_out_4), .out_5(auxiliar_1_out_5));
  Hex_Digit_Display hex_digit_display_1 (.value(auxiliar_1_out_3));  // open: dp
  Hex_Digit_Display hex_digit_display_2 (.value(auxiliar_1_out_4));  // open: dp
  Hex_Digit_Display hex_digit_display_3 (.value(auxiliar_1_out_5));  // open: dp

  // Notes on the sheet:
  //   0 - Positivo
  //   Sinal
  //   Digite o numero em Binário
  //   Operador Aritmético
  //   Chave Seletora
  //   Sinal
  //   Resultado da soma  em Binario
  //   Centena
  //   Unidade
  //   Dezena
  //   Resultado da soma  em Decimal 
endmodule

module Somador (
  input  [7:0] X,
  input  [7:0] Y,
  input  [7:0] W,
  output [7:0] Soma,
  output Resto
);

  wire [7:0] adder_1_out;

  Adder adder_1 (.a(X), .b(Y), .out(adder_1_out), .cin(1'b0));  // open: cout
  Adder adder_2 (.a(adder_1_out), .b(W), .out(Soma), .cin(1'b0), .cout(Resto));
endmodule

module Entrada (
  input  [7:0] in_1,
  input  [3:0] in_2,
  output [7:0] X,
  output [7:0] Y,
  output [7:0] W
);

  D_Flip_Flop d_ff_1 (.clk(in_2[0]), .D(in_1[7]), .Q(X[7]), .reset(in_2[3]));  // open: Qn, preset, en
  D_Flip_Flop d_ff_2 (.clk(in_2[1]), .D(in_1[7]), .Q(Y[7]), .reset(in_2[3]));  // open: Qn, preset, en
  D_Flip_Flop d_ff_3 (.clk(in_2[2]), .D(in_1[7]), .Q(W[7]), .reset(in_2[3]));  // open: Qn, preset, en
  D_Flip_Flop d_ff_4 (.clk(in_2[0]), .D(in_1[6]), .Q(X[6]), .reset(in_2[3]));  // open: Qn, preset, en
  D_Flip_Flop d_ff_5 (.clk(in_2[1]), .D(in_1[6]), .Q(Y[6]), .reset(in_2[3]));  // open: Qn, preset, en
  D_Flip_Flop d_ff_6 (.clk(in_2[2]), .D(in_1[6]), .Q(W[6]), .reset(in_2[3]));  // open: Qn, preset, en
  D_Flip_Flop d_ff_7 (.clk(in_2[0]), .D(in_1[5]), .Q(X[5]), .reset(in_2[3]));  // open: Qn, preset, en
  D_Flip_Flop d_ff_8 (.clk(in_2[1]), .D(in_1[5]), .Q(Y[5]), .reset(in_2[3]));  // open: Qn, preset, en
  D_Flip_Flop d_ff_9 (.clk(in_2[2]), .D(in_1[5]), .Q(W[5]), .reset(in_2[3]));  // open: Qn, preset, en
  D_Flip_Flop d_ff_10 (.clk(in_2[0]), .D(in_1[4]), .Q(X[4]), .reset(in_2[3]));  // open: Qn, preset, en
  D_Flip_Flop d_ff_11 (.clk(in_2[1]), .D(in_1[4]), .Q(Y[4]), .reset(in_2[3]));  // open: Qn, preset, en
  D_Flip_Flop d_ff_12 (.clk(in_2[2]), .D(in_1[4]), .Q(W[4]), .reset(in_2[3]));  // open: Qn, preset, en
  D_Flip_Flop d_ff_13 (.clk(in_2[0]), .D(in_1[3]), .Q(X[3]), .reset(in_2[3]));  // open: Qn, preset, en
  D_Flip_Flop d_ff_14 (.clk(in_2[1]), .D(in_1[3]), .Q(Y[3]), .reset(in_2[3]));  // open: Qn, preset, en
  D_Flip_Flop d_ff_15 (.clk(in_2[2]), .D(in_1[3]), .Q(W[3]), .reset(in_2[3]));  // open: Qn, preset, en
  D_Flip_Flop d_ff_16 (.clk(in_2[0]), .D(in_1[2]), .Q(X[2]), .reset(in_2[3]));  // open: Qn, preset, en
  D_Flip_Flop d_ff_17 (.clk(in_2[1]), .D(in_1[2]), .Q(Y[2]), .reset(in_2[3]));  // open: Qn, preset, en
  D_Flip_Flop d_ff_18 (.clk(in_2[2]), .D(in_1[2]), .Q(W[2]), .reset(in_2[3]));  // open: Qn, preset, en
  D_Flip_Flop d_ff_19 (.clk(in_2[0]), .D(in_1[1]), .Q(X[1]), .reset(in_2[3]));  // open: Qn, preset, en
  D_Flip_Flop d_ff_20 (.clk(in_2[1]), .D(in_1[1]), .Q(Y[1]), .reset(in_2[3]));  // open: Qn, preset, en
  D_Flip_Flop d_ff_21 (.clk(in_2[2]), .D(in_1[1]), .Q(W[1]), .reset(in_2[3]));  // open: Qn, preset, en
  D_Flip_Flop d_ff_22 (.clk(in_2[0]), .D(in_1[0]), .Q(X[0]), .reset(in_2[3]));  // open: Qn, preset, en
  D_Flip_Flop d_ff_23 (.clk(in_2[1]), .D(in_1[0]), .Q(Y[0]), .reset(in_2[3]));  // open: Qn, preset, en
  D_Flip_Flop d_ff_24 (.clk(in_2[2]), .D(in_1[0]), .Q(W[0]), .reset(in_2[3]));  // open: Qn, preset, en
endmodule

// AUX
module Auxiliar (
  input  [7:0] in_1,
  output F1,
  output [3:0] out_3,
  output [3:0] out_4,
  output [3:0] out_5
);

  wire and_1_out, and_2_out, and_3_out, and_4_out, and_5_out, and_6_out, and_7_out, and_8_out, and_9_out,
       and_10_out, and_11_out, and_12_out, and_13_out, and_14_out, and_15_out, and_16_out, and_17_out,
       and_18_out, and_19_out, and_20_out, and_21_out, and_22_out, and_23_out, and_24_out, and_25_out,
       and_26_out, and_27_out, and_28_out, and_29_out, and_30_out, and_31_out, and_32_out, and_33_out,
       and_34_out, and_35_out, and_36_out, and_37_out, and_38_out, and_39_out, and_40_out, and_41_out,
       and_42_out, and_43_out, and_44_out, and_45_out, and_46_out, and_47_out, and_48_out, and_49_out,
       and_50_out, and_51_out, and_52_out, and_53_out, and_54_out, and_55_out, and_56_out, and_57_out,
       and_58_out, and_59_out, and_60_out, and_61_out, and_62_out, and_63_out, and_64_out, and_65_out,
       and_66_out, and_67_out, and_68_out, and_69_out, and_70_out, and_71_out, and_72_out, and_73_out,
       and_74_out, and_75_out, and_76_out, and_77_out, and_78_out, and_79_out, and_80_out, and_81_out,
       and_82_out, and_83_out, and_84_out, and_85_out, and_86_out, and_87_out, and_88_out, and_89_out,
       and_90_out, and_91_out, and_92_out, and_93_out, and_94_out, and_95_out, and_96_out, and_97_out,
       and_98_out, and_99_out, and_100_out, and_101_out, and_102_out, and_103_out, and_104_out, and_105_out,
       and_106_out, and_107_out, and_108_out, and_109_out, and_110_out, and_111_out, and_112_out,
       and_113_out, and_114_out, and_115_out, and_116_out, and_117_out, and_118_out, and_119_out,
       and_120_out, and_121_out, and_122_out, and_123_out, and_124_out, and_125_out, and_126_out,
       and_127_out, and_128_out, and_129_out, and_130_out, and_131_out, and_132_out, and_133_out,
       and_134_out, and_135_out, and_136_out, and_137_out, and_138_out, and_139_out, and_140_out,
       and_141_out, and_142_out, and_143_out, and_144_out, and_145_out, and_146_out, and_147_out,
       and_148_out, and_149_out, and_150_out, and_151_out, and_152_out, and_153_out, and_154_out,
       and_155_out, and_156_out, and_157_out, and_158_out, and_159_out, and_160_out, and_161_out,
       and_162_out, and_163_out, and_164_out, and_165_out, and_166_out, and_167_out, and_168_out,
       and_169_out, and_170_out, and_171_out, and_172_out, and_173_out, and_174_out, and_175_out,
       and_176_out, and_177_out, and_178_out, and_179_out, and_180_out, and_181_out, and_182_out,
       and_183_out, and_184_out, and_185_out, and_186_out, and_187_out, and_188_out, and_189_out,
       and_190_out, and_191_out, and_192_out, and_193_out, and_194_out, and_195_out, and_196_out,
       and_197_out, and_198_out, and_199_out, and_200_out, and_201_out, and_202_out, and_203_out,
       and_204_out, and_205_out, and_206_out, and_207_out, and_208_out, and_209_out, and_210_out,
       and_211_out, not_1_out, not_2_out, not_3_out, not_4_out, not_5_out, not_6_out, not_7_out, not_8_out,
       not_9_out, not_10_out, not_11_out, not_12_out, not_13_out, not_14_out, not_15_out, not_16_out,
       not_17_out, not_18_out, not_19_out, not_20_out, not_21_out, not_22_out, not_23_out, not_24_out,
       not_25_out, not_26_out, not_27_out, not_28_out, not_29_out, not_30_out, not_31_out, not_32_out,
       not_33_out, not_34_out, not_35_out, not_36_out, not_37_out, not_38_out, not_39_out, not_40_out,
       not_41_out, not_42_out, not_43_out, not_44_out, not_45_out, not_46_out, not_47_out, not_48_out,
       not_49_out, not_50_out, not_51_out, not_52_out, not_53_out, not_54_out, not_55_out, not_56_out,
       not_57_out, not_58_out, not_59_out, not_60_out, not_61_out, not_62_out, not_63_out, not_64_out,
       not_65_out, not_66_out, not_67_out, not_68_out, not_69_out, not_70_out, not_71_out, not_72_out,
       not_73_out, not_74_out, not_75_out, not_76_out, not_77_out, not_78_out, not_79_out, not_80_out,
       not_81_out, not_82_out, not_83_out, not_84_out, not_85_out, not_86_out, not_87_out, not_88_out,
       not_89_out, not_90_out, not_91_out, not_92_out, not_93_out, not_94_out, not_95_out, not_96_out,
       not_97_out, not_98_out, not_99_out, not_100_out, not_101_out, not_102_out, not_103_out, not_104_out,
       not_105_out, not_106_out, not_107_out, not_108_out, not_109_out, not_110_out, not_111_out,
       not_112_out, not_113_out, not_114_out, not_115_out, not_116_out, not_117_out, not_118_out,
       not_119_out, not_120_out, not_121_out, not_122_out, not_123_out, not_124_out, not_125_out,
       not_126_out, not_127_out, not_128_out, not_129_out, not_130_out, not_131_out, not_132_out,
       not_133_out, not_134_out, not_135_out, not_136_out, not_137_out, not_138_out, not_139_out,
       not_140_out, not_141_out, not_142_out, not_143_out, not_144_out, not_145_out, not_146_out,
       not_147_out, not_148_out, not_149_out, not_150_out, not_151_out, not_152_out, not_153_out,
       not_154_out, not_155_out, not_156_out, not_157_out, not_158_out, not_159_out, not_160_out,
       not_161_out, not_162_out, not_163_out, not_164_out, not_165_out, not_166_out, not_167_out,
       not_168_out, not_169_out, not_170_out, not_171_out, not_172_out, not_173_out, not_174_out,
       not_175_out, not_176_out, not_177_out, not_178_out, not_179_out, not_180_out, not_181_out,
       not_182_out, not_183_out, not_184_out, not_185_out, not_186_out, not_187_out, not_188_out,
       not_189_out, not_190_out, not_191_out, not_192_out, not_193_out, not_194_out, not_195_out,
       not_196_out, not_197_out, not_198_out, not_199_out, not_200_out, not_201_out, not_202_out,
       not_203_out, not_204_out, not_205_out, not_206_out, not_207_out, not_208_out, not_209_out,
       not_210_out, not_211_out, not_212_out, not_213_out, not_214_out, not_215_out, not_216_out,
       not_217_out, not_218_out, not_219_out, not_220_out, not_221_out, not_222_out, not_223_out,
       not_224_out, not_225_out, not_226_out, not_227_out, not_228_out, not_229_out, not_230_out,
       not_231_out, not_232_out, not_233_out, not_234_out, not_235_out, not_236_out, not_237_out,
       not_238_out, not_239_out, not_240_out, not_241_out, not_242_out, not_243_out, not_244_out,
       not_245_out, not_246_out, not_247_out, not_248_out, not_249_out, not_250_out, not_251_out,
       not_252_out, not_253_out, not_254_out, not_255_out, not_256_out, not_257_out, not_258_out,
       not_259_out, not_260_out, not_261_out, not_262_out, not_263_out, not_264_out, not_265_out,
       not_266_out, not_267_out, not_268_out, not_269_out, not_270_out, not_271_out, not_272_out,
       not_273_out, not_274_out, not_275_out, not_276_out, not_277_out, not_278_out, not_279_out,
       not_280_out, not_281_out, not_282_out, not_283_out, not_284_out, not_285_out, not_286_out,
       not_287_out, not_288_out, not_289_out, not_290_out, not_291_out, not_292_out, not_293_out,
       not_294_out, not_295_out, not_296_out, not_297_out, not_298_out, not_299_out, not_300_out,
       not_301_out, not_302_out, not_303_out, not_304_out, not_305_out, not_306_out, not_307_out,
       not_308_out, not_309_out, not_310_out, not_311_out, not_312_out, not_313_out, not_314_out,
       not_315_out, not_316_out, not_317_out, not_318_out, not_319_out, not_320_out, not_321_out,
       not_322_out, not_323_out, not_324_out, not_325_out, not_326_out, not_327_out, not_328_out,
       not_329_out, not_330_out, not_331_out, not_332_out, not_333_out, not_334_out, not_335_out,
       not_336_out, not_337_out, not_338_out, not_339_out, not_340_out, not_341_out, not_342_out,
       not_343_out, not_344_out, not_345_out, not_346_out, not_347_out, not_348_out, not_349_out,
       not_350_out, not_351_out, not_352_out, not_353_out, not_354_out, not_355_out, not_356_out,
       not_357_out, not_358_out, not_359_out, not_360_out, not_361_out, not_362_out, not_363_out,
       not_364_out, not_365_out, not_366_out, not_367_out, not_368_out, not_369_out, not_370_out,
       not_371_out, not_372_out, not_373_out, not_374_out, not_375_out, not_376_out, not_377_out,
       not_378_out, not_379_out, not_380_out, not_381_out, not_382_out, not_383_out, not_384_out,
       not_385_out, not_386_out, not_387_out, not_388_out, not_389_out, not_390_out, not_391_out,
       not_392_out, not_393_out, not_394_out, not_395_out, not_396_out, not_397_out, not_398_out,
       not_399_out, not_400_out, not_401_out, not_402_out, not_403_out, not_404_out, not_405_out,
       not_406_out, not_407_out, not_408_out, not_409_out, not_410_out, not_411_out, not_412_out,
       not_413_out, not_414_out, not_415_out, not_416_out, not_417_out, not_418_out, not_419_out,
       not_420_out, not_421_out, not_422_out, not_423_out, not_424_out, not_425_out, not_426_out,
       not_427_out, not_428_out, not_429_out, not_430_out, not_431_out, not_432_out, not_433_out,
       not_434_out, not_435_out, not_436_out, not_437_out, not_438_out, not_439_out, not_440_out,
       not_441_out, not_442_out, not_443_out, not_444_out, not_445_out, not_446_out, not_447_out,
       not_448_out, not_449_out, not_450_out, not_451_out, not_452_out, not_453_out, not_454_out,
       not_455_out, not_456_out, not_457_out, not_458_out, not_459_out, not_460_out, not_461_out,
       not_462_out, not_463_out, not_464_out, not_465_out, not_466_out, not_467_out, not_468_out,
       not_469_out, not_470_out, not_471_out, not_472_out, not_473_out, not_474_out, not_475_out,
       not_476_out, not_477_out, not_478_out, not_479_out, not_480_out, not_481_out, not_482_out,
       not_483_out, not_484_out, not_485_out, not_486_out, not_487_out, not_488_out, not_489_out,
       not_490_out, not_491_out, not_492_out, not_493_out, not_494_out, not_495_out, not_496_out,
       not_497_out, not_498_out, not_499_out, not_500_out, not_501_out, not_502_out, not_503_out,
       not_504_out, not_505_out, not_506_out, not_507_out, not_508_out, not_509_out, not_510_out,
       not_511_out, not_512_out, not_513_out, not_514_out, not_515_out, not_516_out, not_517_out,
       not_518_out, not_519_out, not_520_out, not_521_out, not_522_out, not_523_out, not_524_out,
       not_525_out, not_526_out, not_527_out, not_528_out, not_529_out, not_530_out, not_531_out,
       not_532_out, not_533_out, not_534_out, not_535_out, not_536_out, not_537_out, not_538_out,
       not_539_out, not_540_out, not_541_out, not_542_out, not_543_out, not_544_out, not_545_out,
       not_546_out, not_547_out, not_548_out, not_549_out, not_550_out, not_551_out, not_552_out,
       not_553_out, not_554_out, not_555_out, not_556_out, not_557_out, not_558_out, not_559_out,
       not_560_out, not_561_out, not_562_out, not_563_out, not_564_out, not_565_out, not_566_out,
       not_567_out, not_568_out, not_569_out, not_570_out, not_571_out, not_572_out, not_573_out,
       not_574_out, not_575_out, not_576_out, not_577_out, not_578_out, not_579_out, not_580_out,
       not_581_out, not_582_out, not_583_out, not_584_out, not_585_out, not_586_out, not_587_out,
       not_588_out, not_589_out, not_590_out, not_591_out, not_592_out, not_593_out, not_594_out,
       not_595_out, not_596_out, not_597_out, not_598_out, not_599_out, not_600_out, not_601_out,
       not_602_out, not_603_out, not_604_out, not_605_out, not_606_out, not_607_out, not_608_out,
       not_609_out, not_610_out, not_611_out, not_612_out, not_613_out, not_614_out, not_615_out,
       not_616_out, not_617_out, not_618_out, not_619_out, not_620_out, not_621_out, not_622_out,
       not_623_out, not_624_out, not_625_out, not_626_out, not_627_out, not_628_out, not_629_out,
       not_630_out, not_631_out, not_632_out, not_633_out, not_634_out, not_635_out, not_636_out,
       not_637_out, not_638_out, not_639_out, not_640_out, not_641_out, not_642_out, not_643_out,
       not_644_out, not_645_out, not_646_out, not_647_out, not_648_out, or_5_out, or_6_out, or_7_out,
       or_8_out, or_11_out, or_13_out;

  not not_1 (not_1_out, in_1[7]);
  not not_2 (not_2_out, in_1[7]);
  not not_3 (not_3_out, in_1[7]);
  not not_4 (not_4_out, in_1[6]);
  not not_5 (not_5_out, in_1[5]);
  not not_6 (not_6_out, in_1[4]);
  not not_7 (not_7_out, in_1[6]);
  not not_8 (not_8_out, in_1[5]);
  not not_9 (not_9_out, in_1[3]);
  not not_10 (not_10_out, in_1[6]);
  not not_11 (not_11_out, in_1[5]);
  not not_12 (not_12_out, in_1[2]);
  not not_13 (not_13_out, in_1[6]);
  not not_14 (not_14_out, in_1[5]);
  not not_15 (not_15_out, in_1[1]);
  not not_16 (not_16_out, in_1[0]);
  not not_17 (not_17_out, in_1[7]);
  not not_18 (not_18_out, in_1[5]);
  not not_19 (not_19_out, in_1[7]);
  not not_20 (not_20_out, in_1[4]);
  not not_21 (not_21_out, in_1[3]);
  not not_22 (not_22_out, in_1[2]);
  not not_23 (not_23_out, in_1[6]);
  not not_24 (not_24_out, in_1[5]);
  not not_25 (not_25_out, in_1[6]);
  not not_26 (not_26_out, in_1[5]);
  not not_27 (not_27_out, in_1[6]);
  not not_28 (not_28_out, in_1[4]);
  not not_29 (not_29_out, in_1[6]);
  not not_30 (not_30_out, in_1[3]);
  not not_31 (not_31_out, in_1[2]);
  not not_32 (not_32_out, in_1[1]);
  not not_33 (not_33_out, in_1[0]);
  not not_34 (not_34_out, in_1[7]);
  not not_35 (not_35_out, in_1[6]);
  not not_36 (not_36_out, in_1[7]);
  not not_37 (not_37_out, in_1[6]);
  not not_38 (not_38_out, in_1[6]);
  not not_39 (not_39_out, in_1[6]);
  not not_40 (not_40_out, in_1[6]);
  not not_41 (not_41_out, in_1[6]);
  not not_42 (not_42_out, in_1[5]);
  not not_43 (not_43_out, in_1[4]);
  not not_44 (not_44_out, in_1[5]);
  not not_45 (not_45_out, in_1[3]);
  not not_46 (not_46_out, in_1[5]);
  not not_47 (not_47_out, in_1[2]);
  not not_48 (not_48_out, in_1[1]);
  not not_49 (not_49_out, in_1[0]);
  not not_50 (not_50_out, in_1[7]);
  not not_51 (not_51_out, in_1[6]);
  not not_52 (not_52_out, in_1[5]);
  not not_53 (not_53_out, in_1[7]);
  not not_54 (not_54_out, in_1[6]);
  not not_55 (not_55_out, in_1[5]);
  not not_56 (not_56_out, in_1[7]);
  not not_57 (not_57_out, in_1[6]);
  not not_58 (not_58_out, in_1[4]);
  not not_59 (not_59_out, in_1[3]);
  not not_60 (not_60_out, in_1[7]);
  not not_61 (not_61_out, in_1[7]);
  not not_62 (not_62_out, in_1[5]);
  not not_63 (not_63_out, in_1[4]);
  not not_64 (not_64_out, in_1[5]);
  not not_65 (not_65_out, in_1[4]);
  not not_66 (not_66_out, in_1[3]);
  not not_67 (not_67_out, in_1[2]);
  not not_68 (not_68_out, in_1[7]);
  not not_69 (not_69_out, in_1[6]);
  not not_70 (not_70_out, in_1[5]);
  not not_71 (not_71_out, in_1[4]);
  not not_72 (not_72_out, in_1[3]);
  not not_73 (not_73_out, in_1[6]);
  not not_74 (not_74_out, in_1[5]);
  not not_75 (not_75_out, in_1[4]);
  not not_76 (not_76_out, in_1[2]);
  not not_77 (not_77_out, in_1[1]);
  not not_78 (not_78_out, in_1[0]);
  not not_79 (not_79_out, in_1[5]);
  not not_80 (not_80_out, in_1[4]);
  not not_81 (not_81_out, in_1[3]);
  not not_82 (not_82_out, in_1[1]);
  not not_83 (not_83_out, in_1[0]);
  not not_84 (not_84_out, in_1[6]);
  not not_85 (not_85_out, in_1[6]);
  not not_86 (not_86_out, in_1[6]);
  not not_87 (not_87_out, in_1[6]);
  not not_88 (not_88_out, in_1[5]);
  not not_89 (not_89_out, in_1[5]);
  not not_90 (not_90_out, in_1[5]);
  not not_91 (not_91_out, in_1[4]);
  not not_92 (not_92_out, in_1[3]);
  not not_93 (not_93_out, in_1[4]);
  not not_94 (not_94_out, in_1[2]);
  not not_95 (not_95_out, in_1[4]);
  not not_96 (not_96_out, in_1[1]);
  not not_97 (not_97_out, in_1[0]);
  not not_98 (not_98_out, in_1[5]);
  not not_99 (not_99_out, in_1[4]);
  not not_100 (not_100_out, in_1[2]);
  not not_101 (not_101_out, in_1[6]);
  not not_102 (not_102_out, in_1[5]);
  not not_103 (not_103_out, in_1[4]);
  not not_104 (not_104_out, in_1[6]);
  not not_105 (not_105_out, in_1[5]);
  not not_106 (not_106_out, in_1[7]);
  not not_107 (not_107_out, in_1[6]);
  not not_108 (not_108_out, in_1[5]);
  not not_109 (not_109_out, in_1[3]);
  not not_110 (not_110_out, in_1[2]);
  not not_111 (not_111_out, in_1[6]);
  not not_112 (not_112_out, in_1[5]);
  not not_113 (not_113_out, in_1[3]);
  not not_114 (not_114_out, in_1[2]);
  not not_115 (not_115_out, in_1[1]);
  not not_116 (not_116_out, in_1[6]);
  not not_117 (not_117_out, in_1[5]);
  not not_118 (not_118_out, in_1[3]);
  not not_119 (not_119_out, in_1[2]);
  not not_120 (not_120_out, in_1[0]);
  not not_121 (not_121_out, in_1[6]);
  not not_122 (not_122_out, in_1[4]);
  not not_123 (not_123_out, in_1[3]);
  not not_124 (not_124_out, in_1[2]);
  not not_125 (not_125_out, in_1[4]);
  not not_126 (not_126_out, in_1[3]);
  not not_127 (not_127_out, in_1[2]);
  not not_128 (not_128_out, in_1[1]);
  not not_129 (not_129_out, in_1[7]);
  not not_130 (not_130_out, in_1[6]);
  not not_131 (not_131_out, in_1[3]);
  not not_132 (not_132_out, in_1[6]);
  not not_133 (not_133_out, in_1[3]);
  not not_134 (not_134_out, in_1[1]);
  not not_135 (not_135_out, in_1[6]);
  not not_136 (not_136_out, in_1[3]);
  not not_137 (not_137_out, in_1[0]);
  not not_138 (not_138_out, in_1[6]);
  not not_139 (not_139_out, in_1[3]);
  not not_140 (not_140_out, in_1[7]);
  not not_141 (not_141_out, in_1[6]);
  not not_142 (not_142_out, in_1[2]);
  not not_143 (not_143_out, in_1[6]);
  not not_144 (not_144_out, in_1[2]);
  not not_145 (not_145_out, in_1[1]);
  not not_146 (not_146_out, in_1[6]);
  not not_147 (not_147_out, in_1[2]);
  not not_148 (not_148_out, in_1[0]);
  not not_149 (not_149_out, in_1[5]);
  not not_150 (not_150_out, in_1[4]);
  not not_151 (not_151_out, in_1[3]);
  not not_152 (not_152_out, in_1[5]);
  not not_153 (not_153_out, in_1[4]);
  not not_154 (not_154_out, in_1[1]);
  not not_155 (not_155_out, in_1[7]);
  not not_156 (not_156_out, in_1[5]);
  not not_157 (not_157_out, in_1[5]);
  not not_158 (not_158_out, in_1[0]);
  not not_159 (not_159_out, in_1[5]);
  not not_160 (not_160_out, in_1[7]);
  not not_161 (not_161_out, in_1[3]);
  not not_162 (not_162_out, in_1[2]);
  not not_163 (not_163_out, in_1[3]);
  not not_164 (not_164_out, in_1[2]);
  not not_165 (not_165_out, in_1[0]);
  not not_166 (not_166_out, in_1[4]);
  not not_167 (not_167_out, in_1[4]);
  not not_168 (not_168_out, in_1[7]);
  not not_169 (not_169_out, in_1[3]);
  not not_170 (not_170_out, in_1[3]);
  not not_171 (not_171_out, in_1[1]);
  not not_172 (not_172_out, in_1[3]);
  not not_173 (not_173_out, in_1[0]);
  not not_174 (not_174_out, in_1[5]);
  not not_175 (not_175_out, in_1[4]);
  not not_176 (not_176_out, in_1[1]);
  not not_177 (not_177_out, in_1[6]);
  not not_178 (not_178_out, in_1[5]);
  not not_179 (not_179_out, in_1[3]);
  not not_180 (not_180_out, in_1[2]);
  not not_181 (not_181_out, in_1[5]);
  not not_182 (not_182_out, in_1[4]);
  not not_183 (not_183_out, in_1[1]);
  not not_184 (not_184_out, in_1[5]);
  not not_185 (not_185_out, in_1[7]);
  not not_186 (not_186_out, in_1[6]);
  not not_187 (not_187_out, in_1[5]);
  not not_188 (not_188_out, in_1[4]);
  not not_189 (not_189_out, in_1[2]);
  not not_190 (not_190_out, in_1[1]);
  not not_191 (not_191_out, in_1[6]);
  not not_192 (not_192_out, in_1[5]);
  not not_193 (not_193_out, in_1[4]);
  not not_194 (not_194_out, in_1[2]);
  not not_195 (not_195_out, in_1[1]);
  not not_196 (not_196_out, in_1[7]);
  not not_197 (not_197_out, in_1[6]);
  not not_198 (not_198_out, in_1[5]);
  not not_199 (not_199_out, in_1[3]);
  not not_200 (not_200_out, in_1[2]);
  not not_201 (not_201_out, in_1[6]);
  not not_202 (not_202_out, in_1[5]);
  not not_203 (not_203_out, in_1[3]);
  not not_204 (not_204_out, in_1[2]);
  not not_205 (not_205_out, in_1[7]);
  not not_206 (not_206_out, in_1[6]);
  not not_207 (not_207_out, in_1[5]);
  not not_208 (not_208_out, in_1[1]);
  not not_209 (not_209_out, in_1[6]);
  not not_210 (not_210_out, in_1[5]);
  not not_211 (not_211_out, in_1[1]);
  not not_212 (not_212_out, in_1[7]);
  not not_213 (not_213_out, in_1[6]);
  not not_214 (not_214_out, in_1[4]);
  not not_215 (not_215_out, in_1[3]);
  not not_216 (not_216_out, in_1[6]);
  not not_217 (not_217_out, in_1[4]);
  not not_218 (not_218_out, in_1[3]);
  not not_219 (not_219_out, in_1[7]);
  not not_220 (not_220_out, in_1[6]);
  not not_221 (not_221_out, in_1[3]);
  not not_222 (not_222_out, in_1[2]);
  not not_223 (not_223_out, in_1[1]);
  not not_224 (not_224_out, in_1[6]);
  not not_225 (not_225_out, in_1[3]);
  not not_226 (not_226_out, in_1[2]);
  not not_227 (not_227_out, in_1[1]);
  not not_228 (not_228_out, in_1[7]);
  not not_229 (not_229_out, in_1[6]);
  not not_230 (not_230_out, in_1[2]);
  not not_231 (not_231_out, in_1[6]);
  not not_232 (not_232_out, in_1[2]);
  not not_233 (not_233_out, in_1[7]);
  not not_234 (not_234_out, in_1[5]);
  not not_235 (not_235_out, in_1[4]);
  not not_236 (not_236_out, in_1[3]);
  not not_237 (not_237_out, in_1[1]);
  not not_238 (not_238_out, in_1[5]);
  not not_239 (not_239_out, in_1[4]);
  not not_240 (not_240_out, in_1[3]);
  not not_241 (not_241_out, in_1[1]);
  not not_242 (not_242_out, in_1[7]);
  not not_243 (not_243_out, in_1[5]);
  not not_244 (not_244_out, in_1[4]);
  not not_245 (not_245_out, in_1[5]);
  not not_246 (not_246_out, in_1[4]);
  not not_247 (not_247_out, in_1[7]);
  not not_248 (not_248_out, in_1[5]);
  not not_249 (not_249_out, in_1[2]);
  not not_250 (not_250_out, in_1[1]);
  not not_251 (not_251_out, in_1[5]);
  not not_252 (not_252_out, in_1[2]);
  not not_253 (not_253_out, in_1[1]);
  not not_254 (not_254_out, in_1[7]);
  not not_255 (not_255_out, in_1[4]);
  not not_256 (not_256_out, in_1[3]);
  not not_257 (not_257_out, in_1[2]);
  not not_258 (not_258_out, in_1[4]);
  not not_259 (not_259_out, in_1[3]);
  not not_260 (not_260_out, in_1[2]);
  not not_261 (not_261_out, in_1[7]);
  not not_262 (not_262_out, in_1[4]);
  not not_263 (not_263_out, in_1[1]);
  not not_264 (not_264_out, in_1[4]);
  not not_265 (not_265_out, in_1[1]);
  not not_266 (not_266_out, in_1[7]);
  not not_267 (not_267_out, in_1[3]);
  not not_268 (not_268_out, in_1[3]);
  not not_269 (not_269_out, in_1[6]);
  not not_270 (not_270_out, in_1[5]);
  not not_271 (not_271_out, in_1[4]);
  not not_272 (not_272_out, in_1[3]);
  not not_273 (not_273_out, in_1[2]);
  not not_274 (not_274_out, in_1[1]);
  not not_275 (not_275_out, in_1[0]);
  not not_276 (not_276_out, in_1[6]);
  not not_277 (not_277_out, in_1[5]);
  not not_278 (not_278_out, in_1[4]);
  not not_279 (not_279_out, in_1[2]);
  not not_280 (not_280_out, in_1[0]);
  not not_281 (not_281_out, in_1[6]);
  not not_282 (not_282_out, in_1[5]);
  not not_283 (not_283_out, in_1[3]);
  not not_284 (not_284_out, in_1[1]);
  not not_285 (not_285_out, in_1[0]);
  not not_286 (not_286_out, in_1[6]);
  not not_287 (not_287_out, in_1[5]);
  not not_288 (not_288_out, in_1[0]);
  not not_289 (not_289_out, in_1[6]);
  not not_290 (not_290_out, in_1[4]);
  not not_291 (not_291_out, in_1[2]);
  not not_292 (not_292_out, in_1[1]);
  not not_293 (not_293_out, in_1[0]);
  not not_294 (not_294_out, in_1[6]);
  not not_295 (not_295_out, in_1[3]);
  not not_296 (not_296_out, in_1[2]);
  not not_297 (not_297_out, in_1[0]);
  not not_298 (not_298_out, in_1[6]);
  not not_299 (not_299_out, in_1[1]);
  not not_300 (not_300_out, in_1[0]);
  not not_301 (not_301_out, in_1[5]);
  not not_302 (not_302_out, in_1[4]);
  not not_303 (not_303_out, in_1[3]);
  not not_304 (not_304_out, in_1[0]);
  not not_305 (not_305_out, in_1[5]);
  not not_306 (not_306_out, in_1[3]);
  not not_307 (not_307_out, in_1[2]);
  not not_308 (not_308_out, in_1[1]);
  not not_309 (not_309_out, in_1[0]);
  not not_310 (not_310_out, in_1[5]);
  not not_311 (not_311_out, in_1[2]);
  not not_312 (not_312_out, in_1[0]);
  not not_313 (not_313_out, in_1[4]);
  not not_314 (not_314_out, in_1[3]);
  not not_315 (not_315_out, in_1[1]);
  not not_316 (not_316_out, in_1[0]);
  not not_317 (not_317_out, in_1[4]);
  not not_318 (not_318_out, in_1[0]);
  not not_319 (not_319_out, in_1[2]);
  not not_320 (not_320_out, in_1[1]);
  not not_321 (not_321_out, in_1[0]);
  not not_322 (not_322_out, in_1[7]);
  not not_323 (not_323_out, in_1[6]);
  not not_324 (not_324_out, in_1[4]);
  not not_325 (not_325_out, in_1[3]);
  not not_326 (not_326_out, in_1[1]);
  not not_327 (not_327_out, in_1[7]);
  not not_328 (not_328_out, in_1[6]);
  not not_329 (not_329_out, in_1[5]);
  not not_330 (not_330_out, in_1[4]);
  not not_331 (not_331_out, in_1[6]);
  not not_332 (not_332_out, in_1[5]);
  not not_333 (not_333_out, in_1[4]);
  not not_334 (not_334_out, in_1[0]);
  not not_335 (not_335_out, in_1[7]);
  not not_336 (not_336_out, in_1[6]);
  not not_337 (not_337_out, in_1[5]);
  not not_338 (not_338_out, in_1[2]);
  not not_339 (not_339_out, in_1[1]);
  not not_340 (not_340_out, in_1[7]);
  not not_341 (not_341_out, in_1[6]);
  not not_342 (not_342_out, in_1[5]);
  not not_343 (not_343_out, in_1[2]);
  not not_344 (not_344_out, in_1[7]);
  not not_345 (not_345_out, in_1[6]);
  not not_346 (not_346_out, in_1[2]);
  not not_347 (not_347_out, in_1[1]);
  not not_348 (not_348_out, in_1[6]);
  not not_349 (not_349_out, in_1[5]);
  not not_350 (not_350_out, in_1[2]);
  not not_351 (not_351_out, in_1[1]);
  not not_352 (not_352_out, in_1[0]);
  not not_353 (not_353_out, in_1[7]);
  not not_354 (not_354_out, in_1[6]);
  not not_355 (not_355_out, in_1[4]);
  not not_356 (not_356_out, in_1[3]);
  not not_357 (not_357_out, in_1[2]);
  not not_358 (not_358_out, in_1[7]);
  not not_359 (not_359_out, in_1[6]);
  not not_360 (not_360_out, in_1[4]);
  not not_361 (not_361_out, in_1[7]);
  not not_362 (not_362_out, in_1[6]);
  not not_363 (not_363_out, in_1[3]);
  not not_364 (not_364_out, in_1[7]);
  not not_365 (not_365_out, in_1[4]);
  not not_366 (not_366_out, in_1[3]);
  not not_367 (not_367_out, in_1[2]);
  not not_368 (not_368_out, in_1[1]);
  not not_369 (not_369_out, in_1[7]);
  not not_370 (not_370_out, in_1[5]);
  not not_371 (not_371_out, in_1[4]);
  not not_372 (not_372_out, in_1[2]);
  not not_373 (not_373_out, in_1[5]);
  not not_374 (not_374_out, in_1[4]);
  not not_375 (not_375_out, in_1[2]);
  not not_376 (not_376_out, in_1[0]);
  not not_377 (not_377_out, in_1[7]);
  not not_378 (not_378_out, in_1[5]);
  not not_379 (not_379_out, in_1[4]);
  not not_380 (not_380_out, in_1[1]);
  not not_381 (not_381_out, in_1[7]);
  not not_382 (not_382_out, in_1[3]);
  not not_383 (not_383_out, in_1[1]);
  not not_384 (not_384_out, in_1[5]);
  not not_385 (not_385_out, in_1[3]);
  not not_386 (not_386_out, in_1[1]);
  not not_387 (not_387_out, in_1[0]);
  not not_388 (not_388_out, in_1[7]);
  not not_389 (not_389_out, in_1[5]);
  not not_390 (not_390_out, in_1[5]);
  not not_391 (not_391_out, in_1[0]);
  not not_392 (not_392_out, in_1[7]);
  not not_393 (not_393_out, in_1[4]);
  not not_394 (not_394_out, in_1[2]);
  not not_395 (not_395_out, in_1[7]);
  not not_396 (not_396_out, in_1[3]);
  not not_397 (not_397_out, in_1[2]);
  not not_398 (not_398_out, in_1[7]);
  not not_399 (not_399_out, in_1[1]);
  not not_400 (not_400_out, in_1[0]);
  not not_401 (not_401_out, in_1[6]);
  not not_402 (not_402_out, in_1[4]);
  not not_403 (not_403_out, in_1[3]);
  not not_404 (not_404_out, in_1[2]);
  not not_405 (not_405_out, in_1[1]);
  not not_406 (not_406_out, in_1[6]);
  not not_407 (not_407_out, in_1[5]);
  not not_408 (not_408_out, in_1[4]);
  not not_409 (not_409_out, in_1[3]);
  not not_410 (not_410_out, in_1[2]);
  not not_411 (not_411_out, in_1[6]);
  not not_412 (not_412_out, in_1[5]);
  not not_413 (not_413_out, in_1[4]);
  not not_414 (not_414_out, in_1[2]);
  not not_415 (not_415_out, in_1[6]);
  not not_416 (not_416_out, in_1[5]);
  not not_417 (not_417_out, in_1[4]);
  not not_418 (not_418_out, in_1[1]);
  not not_419 (not_419_out, in_1[0]);
  not not_420 (not_420_out, in_1[6]);
  not not_421 (not_421_out, in_1[5]);
  not not_422 (not_422_out, in_1[4]);
  not not_423 (not_423_out, in_1[1]);
  not not_424 (not_424_out, in_1[6]);
  not not_425 (not_425_out, in_1[4]);
  not not_426 (not_426_out, in_1[1]);
  not not_427 (not_427_out, in_1[0]);
  not not_428 (not_428_out, in_1[6]);
  not not_429 (not_429_out, in_1[3]);
  not not_430 (not_430_out, in_1[1]);
  not not_431 (not_431_out, in_1[6]);
  not not_432 (not_432_out, in_1[5]);
  not not_433 (not_433_out, in_1[3]);
  not not_434 (not_434_out, in_1[6]);
  not not_435 (not_435_out, in_1[5]);
  not not_436 (not_436_out, in_1[6]);
  not not_437 (not_437_out, in_1[4]);
  not not_438 (not_438_out, in_1[3]);
  not not_439 (not_439_out, in_1[2]);
  not not_440 (not_440_out, in_1[0]);
  not not_441 (not_441_out, in_1[6]);
  not not_442 (not_442_out, in_1[4]);
  not not_443 (not_443_out, in_1[2]);
  not not_444 (not_444_out, in_1[0]);
  not not_445 (not_445_out, in_1[6]);
  not not_446 (not_446_out, in_1[4]);
  not not_447 (not_447_out, in_1[2]);
  not not_448 (not_448_out, in_1[6]);
  not not_449 (not_449_out, in_1[3]);
  not not_450 (not_450_out, in_1[2]);
  not not_451 (not_451_out, in_1[6]);
  not not_452 (not_452_out, in_1[3]);
  not not_453 (not_453_out, in_1[0]);
  not not_454 (not_454_out, in_1[6]);
  not not_455 (not_455_out, in_1[6]);
  not not_456 (not_456_out, in_1[5]);
  not not_457 (not_457_out, in_1[4]);
  not not_458 (not_458_out, in_1[2]);
  not not_459 (not_459_out, in_1[1]);
  not not_460 (not_460_out, in_1[0]);
  not not_461 (not_461_out, in_1[4]);
  not not_462 (not_462_out, in_1[3]);
  not not_463 (not_463_out, in_1[5]);
  not not_464 (not_464_out, in_1[4]);
  not not_465 (not_465_out, in_1[2]);
  not not_466 (not_466_out, in_1[1]);
  not not_467 (not_467_out, in_1[4]);
  not not_468 (not_468_out, in_1[2]);
  not not_469 (not_469_out, in_1[1]);
  not not_470 (not_470_out, in_1[0]);
  not not_471 (not_471_out, in_1[3]);
  not not_472 (not_472_out, in_1[2]);
  not not_473 (not_473_out, in_1[1]);
  not not_474 (not_474_out, in_1[5]);
  not not_475 (not_475_out, in_1[3]);
  not not_476 (not_476_out, in_1[2]);
  not not_477 (not_477_out, in_1[5]);
  not not_478 (not_478_out, in_1[2]);
  not not_479 (not_479_out, in_1[5]);
  not not_480 (not_480_out, in_1[1]);
  not not_481 (not_481_out, in_1[4]);
  not not_482 (not_482_out, in_1[3]);
  not not_483 (not_483_out, in_1[4]);
  not not_484 (not_484_out, in_1[3]);
  not not_485 (not_485_out, in_1[4]);
  not not_486 (not_486_out, in_1[3]);
  not not_487 (not_487_out, in_1[2]);
  not not_488 (not_488_out, in_1[0]);
  not not_489 (not_489_out, in_1[2]);
  not not_490 (not_490_out, in_1[2]);
  not not_491 (not_491_out, in_1[7]);
  not not_492 (not_492_out, in_1[5]);
  not not_493 (not_493_out, in_1[4]);
  not not_494 (not_494_out, in_1[3]);
  not not_495 (not_495_out, in_1[2]);
  not not_496 (not_496_out, in_1[5]);
  not not_497 (not_497_out, in_1[4]);
  not not_498 (not_498_out, in_1[3]);
  not not_499 (not_499_out, in_1[2]);
  not not_500 (not_500_out, in_1[0]);
  not not_501 (not_501_out, in_1[7]);
  not not_502 (not_502_out, in_1[6]);
  not not_503 (not_503_out, in_1[5]);
  not not_504 (not_504_out, in_1[3]);
  not not_505 (not_505_out, in_1[6]);
  not not_506 (not_506_out, in_1[5]);
  not not_507 (not_507_out, in_1[3]);
  not not_508 (not_508_out, in_1[0]);
  not not_509 (not_509_out, in_1[7]);
  not not_510 (not_510_out, in_1[5]);
  not not_511 (not_511_out, in_1[4]);
  not not_512 (not_512_out, in_1[1]);
  not not_513 (not_513_out, in_1[5]);
  not not_514 (not_514_out, in_1[4]);
  not not_515 (not_515_out, in_1[1]);
  not not_516 (not_516_out, in_1[0]);
  not not_517 (not_517_out, in_1[7]);
  not not_518 (not_518_out, in_1[6]);
  not not_519 (not_519_out, in_1[5]);
  not not_520 (not_520_out, in_1[3]);
  not not_521 (not_521_out, in_1[2]);
  not not_522 (not_522_out, in_1[1]);
  not not_523 (not_523_out, in_1[6]);
  not not_524 (not_524_out, in_1[5]);
  not not_525 (not_525_out, in_1[3]);
  not not_526 (not_526_out, in_1[2]);
  not not_527 (not_527_out, in_1[1]);
  not not_528 (not_528_out, in_1[0]);
  not not_529 (not_529_out, in_1[7]);
  not not_530 (not_530_out, in_1[6]);
  not not_531 (not_531_out, in_1[5]);
  not not_532 (not_532_out, in_1[2]);
  not not_533 (not_533_out, in_1[6]);
  not not_534 (not_534_out, in_1[5]);
  not not_535 (not_535_out, in_1[2]);
  not not_536 (not_536_out, in_1[0]);
  not not_537 (not_537_out, in_1[7]);
  not not_538 (not_538_out, in_1[4]);
  not not_539 (not_539_out, in_1[3]);
  not not_540 (not_540_out, in_1[2]);
  not not_541 (not_541_out, in_1[1]);
  not not_542 (not_542_out, in_1[4]);
  not not_543 (not_543_out, in_1[3]);
  not not_544 (not_544_out, in_1[2]);
  not not_545 (not_545_out, in_1[1]);
  not not_546 (not_546_out, in_1[0]);
  not not_547 (not_547_out, in_1[7]);
  not not_548 (not_548_out, in_1[6]);
  not not_549 (not_549_out, in_1[3]);
  not not_550 (not_550_out, in_1[1]);
  not not_551 (not_551_out, in_1[6]);
  not not_552 (not_552_out, in_1[3]);
  not not_553 (not_553_out, in_1[1]);
  not not_554 (not_554_out, in_1[0]);
  not not_555 (not_555_out, in_1[7]);
  not not_556 (not_556_out, in_1[4]);
  not not_557 (not_557_out, in_1[2]);
  not not_558 (not_558_out, in_1[4]);
  not not_559 (not_559_out, in_1[2]);
  not not_560 (not_560_out, in_1[0]);
  not not_561 (not_561_out, in_1[7]);
  not not_562 (not_562_out, in_1[6]);
  not not_563 (not_563_out, in_1[6]);
  not not_564 (not_564_out, in_1[0]);
  not not_565 (not_565_out, in_1[7]);
  not not_566 (not_566_out, in_1[6]);
  not not_567 (not_567_out, in_1[2]);
  not not_568 (not_568_out, in_1[1]);
  not not_569 (not_569_out, in_1[6]);
  not not_570 (not_570_out, in_1[2]);
  not not_571 (not_571_out, in_1[1]);
  not not_572 (not_572_out, in_1[0]);
  not not_573 (not_573_out, in_1[7]);
  not not_574 (not_574_out, in_1[5]);
  not not_575 (not_575_out, in_1[4]);
  not not_576 (not_576_out, in_1[1]);
  not not_577 (not_577_out, in_1[5]);
  not not_578 (not_578_out, in_1[4]);
  not not_579 (not_579_out, in_1[1]);
  not not_580 (not_580_out, in_1[0]);
  not not_581 (not_581_out, in_1[7]);
  not not_582 (not_582_out, in_1[5]);
  not not_583 (not_583_out, in_1[1]);
  not not_584 (not_584_out, in_1[5]);
  not not_585 (not_585_out, in_1[1]);
  not not_586 (not_586_out, in_1[0]);
  not not_587 (not_587_out, in_1[7]);
  not not_588 (not_588_out, in_1[5]);
  not not_589 (not_589_out, in_1[3]);
  not not_590 (not_590_out, in_1[5]);
  not not_591 (not_591_out, in_1[3]);
  not not_592 (not_592_out, in_1[0]);
  not not_593 (not_593_out, in_1[7]);
  not not_594 (not_594_out, in_1[4]);
  not not_595 (not_595_out, in_1[3]);
  not not_596 (not_596_out, in_1[4]);
  not not_597 (not_597_out, in_1[3]);
  not not_598 (not_598_out, in_1[0]);
  not not_599 (not_599_out, in_1[7]);
  not not_600 (not_600_out, in_1[3]);
  not not_601 (not_601_out, in_1[1]);
  not not_602 (not_602_out, in_1[3]);
  not not_603 (not_603_out, in_1[1]);
  not not_604 (not_604_out, in_1[0]);
  not not_605 (not_605_out, in_1[7]);
  not not_606 (not_606_out, in_1[0]);
  not not_607 (not_607_out, in_1[5]);
  not not_608 (not_608_out, in_1[4]);
  not not_609 (not_609_out, in_1[3]);
  not not_610 (not_610_out, in_1[2]);
  not not_611 (not_611_out, in_1[1]);
  not not_612 (not_612_out, in_1[6]);
  not not_613 (not_613_out, in_1[5]);
  not not_614 (not_614_out, in_1[3]);
  not not_615 (not_615_out, in_1[1]);
  not not_616 (not_616_out, in_1[5]);
  not not_617 (not_617_out, in_1[4]);
  not not_618 (not_618_out, in_1[2]);
  not not_619 (not_619_out, in_1[6]);
  not not_620 (not_620_out, in_1[5]);
  not not_621 (not_621_out, in_1[6]);
  not not_622 (not_622_out, in_1[5]);
  not not_623 (not_623_out, in_1[2]);
  not not_624 (not_624_out, in_1[1]);
  not not_625 (not_625_out, in_1[6]);
  not not_626 (not_626_out, in_1[3]);
  not not_627 (not_627_out, in_1[2]);
  not not_628 (not_628_out, in_1[4]);
  not not_629 (not_629_out, in_1[2]);
  not not_630 (not_630_out, in_1[1]);
  not not_631 (not_631_out, in_1[6]);
  not not_632 (not_632_out, in_1[1]);
  not not_633 (not_633_out, in_1[6]);
  not not_634 (not_634_out, in_1[3]);
  not not_635 (not_635_out, in_1[3]);
  not not_636 (not_636_out, in_1[2]);
  not not_637 (not_637_out, in_1[5]);
  not not_638 (not_638_out, in_1[4]);
  not not_639 (not_639_out, in_1[3]);
  not not_640 (not_640_out, in_1[5]);
  not not_641 (not_641_out, in_1[3]);
  not not_642 (not_642_out, in_1[1]);
  not not_643 (not_643_out, in_1[5]);
  not not_644 (not_644_out, in_1[4]);
  not not_645 (not_645_out, in_1[3]);
  not not_646 (not_646_out, in_1[1]);
  not not_647 (not_647_out, in_1[4]);
  not not_648 (not_648_out, in_1[1]);
  and and_1 (and_1_out, not_1_out, in_1[6], in_1[5], in_1[2]);
  and and_2 (and_2_out, not_2_out, in_1[6], in_1[5], in_1[3]);
  and and_3 (and_3_out, not_3_out, in_1[6], in_1[5], in_1[4]);
  and and_4 (and_4_out, in_1[7], not_4_out, not_5_out, not_6_out);
  and and_5 (and_5_out, in_1[7], not_7_out, not_8_out, not_9_out);
  and and_6 (and_6_out, in_1[7], not_10_out, not_11_out, not_12_out);
  and and_7 (and_7_out, in_1[7], not_13_out, not_14_out, not_15_out, not_16_out);
  and and_8 (and_8_out, not_17_out, in_1[6], not_18_out, in_1[4]);
  and and_9 (and_9_out, not_19_out, in_1[6], in_1[5], not_20_out, not_21_out, not_22_out);
  and and_10 (and_10_out, in_1[7], not_23_out, not_24_out, in_1[4], in_1[3], in_1[2], in_1[0]);
  and and_11 (and_11_out, in_1[7], not_25_out, not_26_out, in_1[4], in_1[3], in_1[2], in_1[1]);
  and and_12 (and_12_out, in_1[7], not_27_out, in_1[5], not_28_out);
  and and_13 (and_13_out, in_1[7], not_29_out, in_1[5], not_30_out, not_31_out, not_32_out, not_33_out);
  and and_14 (and_14_out, not_34_out, not_35_out, in_1[5], in_1[3]);
  and and_15 (and_15_out, not_36_out, not_37_out, in_1[5], in_1[4]);
  and and_16 (and_16_out, not_38_out, in_1[5], in_1[4], in_1[0]);
  and and_17 (and_17_out, not_39_out, in_1[5], in_1[4], in_1[1]);
  and and_18 (and_18_out, not_40_out, in_1[5], in_1[4], in_1[2]);
  and and_19 (and_19_out, not_41_out, in_1[5], in_1[4], in_1[3]);
  and and_20 (and_20_out, in_1[6], not_42_out, not_43_out);
  and and_21 (and_21_out, in_1[7], in_1[6], not_44_out, not_45_out);
  and and_22 (and_22_out, in_1[7], in_1[6], not_46_out, not_47_out, not_48_out, not_49_out);
  and and_23 (and_23_out, not_50_out, not_51_out, not_52_out, in_1[4], in_1[2]);
  and and_24 (and_24_out, not_53_out, not_54_out, not_55_out, in_1[4], in_1[3]);
  and and_25 (and_25_out, not_56_out, not_57_out, in_1[5], not_58_out, not_59_out);
  and and_26 (and_26_out, not_60_out, in_1[5], in_1[4], in_1[3], in_1[2]);
  and and_27 (and_27_out, not_61_out, in_1[6], not_62_out, not_63_out);
  and and_28 (and_28_out, in_1[6], not_64_out, not_65_out, not_66_out, not_67_out);
  and and_29 (and_29_out, not_68_out, in_1[6], in_1[5], in_1[4], in_1[3]);
  and and_30 (and_30_out, in_1[7], not_69_out, not_70_out, not_71_out, not_72_out);
  and and_31 (and_31_out, in_1[7], not_73_out, not_74_out, not_75_out, not_76_out, not_77_out, not_78_out);
  and and_32 (and_32_out, in_1[7], not_79_out, not_80_out, not_81_out, not_82_out, not_83_out);
  and and_33 (and_33_out, in_1[7], not_84_out, in_1[5], in_1[4], in_1[0]);
  and and_34 (and_34_out, in_1[7], not_85_out, in_1[5], in_1[4], in_1[1]);
  and and_35 (and_35_out, in_1[7], not_86_out, in_1[5], in_1[4], in_1[2]);
  and and_36 (and_36_out, in_1[7], not_87_out, in_1[5], in_1[4], in_1[3]);
  and and_37 (and_37_out, in_1[7], in_1[6], not_88_out, in_1[4], in_1[3], in_1[0]);
  and and_38 (and_38_out, in_1[7], in_1[6], not_89_out, in_1[4], in_1[3], in_1[1]);
  and and_39 (and_39_out, in_1[7], in_1[6], not_90_out, in_1[4], in_1[3], in_1[2]);
  and and_40 (and_40_out, in_1[7], in_1[6], in_1[5], not_91_out, not_92_out);
  and and_41 (and_41_out, in_1[7], in_1[6], in_1[5], not_93_out, not_94_out);
  and and_42 (and_42_out, in_1[7], in_1[6], in_1[5], not_95_out, not_96_out, not_97_out);
  and and_43 (and_43_out, not_98_out, not_99_out, in_1[3], not_100_out, in_1[1]);
  and and_44 (and_44_out, not_101_out, not_102_out, not_103_out, in_1[3], in_1[2]);
  and and_45 (and_45_out, not_104_out, not_105_out, in_1[3], in_1[2], in_1[1]);
  and and_46 (and_46_out, not_106_out, not_107_out, not_108_out, in_1[4], not_109_out, not_110_out);
  and and_47 (and_47_out, not_111_out, not_112_out, in_1[4], not_113_out, not_114_out, not_115_out);
  and and_48 (and_48_out, not_116_out, not_117_out, in_1[4], not_118_out, not_119_out, not_120_out);
  and and_49 (and_49_out, not_121_out, in_1[5], not_122_out, not_123_out, not_124_out);
  and and_50 (and_50_out, in_1[5], not_125_out, not_126_out, not_127_out, not_128_out);
  and and_51 (and_51_out, not_129_out, not_130_out, in_1[5], not_131_out, in_1[2]);
  and and_52 (and_52_out, not_132_out, in_1[5], not_133_out, in_1[2], not_134_out);
  and and_53 (and_53_out, not_135_out, in_1[5], not_136_out, in_1[2], not_137_out);
  and and_54 (and_54_out, not_138_out, in_1[5], in_1[4], not_139_out, in_1[1]);
  and and_55 (and_55_out, not_140_out, not_141_out, in_1[5], in_1[4], in_1[3], not_142_out);
  and and_56 (and_56_out, not_143_out, in_1[5], in_1[4], in_1[3], not_144_out, not_145_out);
  and and_57 (and_57_out, not_146_out, in_1[5], in_1[4], in_1[3], not_147_out, not_148_out);
  and and_58 (and_58_out, in_1[6], not_149_out, not_150_out, not_151_out, in_1[2], in_1[1]);
  and and_59 (and_59_out, in_1[6], not_152_out, not_153_out, in_1[3], not_154_out);
  and and_60 (and_60_out, not_155_out, in_1[6], not_156_out, in_1[3], in_1[1]);
  and and_61 (and_61_out, in_1[6], not_157_out, in_1[3], in_1[1], not_158_out);
  and and_62 (and_62_out, in_1[6], not_159_out, in_1[4], in_1[3], in_1[2]);
  and and_63 (and_63_out, not_160_out, in_1[6], in_1[5], not_161_out, not_162_out);
  and and_64 (and_64_out, in_1[6], in_1[5], not_163_out, not_164_out, not_165_out);
  and and_65 (and_65_out, in_1[6], in_1[5], not_166_out, in_1[3], in_1[2], in_1[0]);
  and and_66 (and_66_out, in_1[6], in_1[5], not_167_out, in_1[3], in_1[2], in_1[1]);
  and and_67 (and_67_out, not_168_out, in_1[6], in_1[5], in_1[4], not_169_out);
  and and_68 (and_68_out, in_1[6], in_1[5], in_1[4], not_170_out, not_171_out);
  and and_69 (and_69_out, in_1[6], in_1[5], in_1[4], not_172_out, not_173_out);
  and and_70 (and_70_out, in_1[7], not_174_out, not_175_out, in_1[3], not_176_out, in_1[0]);
  and and_71 (and_71_out, in_1[7], not_177_out, not_178_out, in_1[3], in_1[2], in_1[0]);
  and and_72 (and_72_out, in_1[7], in_1[5], in_1[4], not_179_out, not_180_out, in_1[0]);
  and and_73 (and_73_out, in_1[7], in_1[6], not_181_out, not_182_out, in_1[2], not_183_out, in_1[0]);
  and and_74 (and_74_out, in_1[7], in_1[6], not_184_out, in_1[4], in_1[3], in_1[0]);
  and and_75 (and_75_out, not_185_out, not_186_out, not_187_out, not_188_out, in_1[3], not_189_out, not_190_out);
  and and_76 (and_76_out, not_191_out, not_192_out, not_193_out, in_1[3], not_194_out, not_195_out, in_1[0]);
  and and_77 (and_77_out, not_196_out, not_197_out, not_198_out, in_1[4], not_199_out, not_200_out, in_1[1]);
  and and_78 (and_78_out, not_201_out, not_202_out, in_1[4], not_203_out, not_204_out, in_1[1], in_1[0]);
  and and_79 (and_79_out, not_205_out, not_206_out, not_207_out, in_1[4], in_1[3], in_1[2], not_208_out);
  and and_80 (and_80_out, not_209_out, not_210_out, in_1[4], in_1[3], in_1[2], not_211_out, in_1[0]);
  and and_81 (and_81_out, not_212_out, not_213_out, in_1[5], not_214_out, not_215_out, in_1[2], in_1[1]);
  and and_82 (and_82_out, not_216_out, in_1[5], not_217_out, not_218_out, in_1[2], in_1[1], in_1[0]);
  and and_83 (and_83_out, not_219_out, not_220_out, in_1[5], in_1[4], not_221_out, not_222_out, not_223_out);
  and and_84 (and_84_out, not_224_out, in_1[5], in_1[4], not_225_out, not_226_out, not_227_out, in_1[0]);
  and and_85 (and_85_out, not_228_out, not_229_out, in_1[5], in_1[4], in_1[3], not_230_out, in_1[1]);
  and and_86 (and_86_out, not_231_out, in_1[5], in_1[4], in_1[3], not_232_out, in_1[1], in_1[0]);
  and and_87 (and_87_out, not_233_out, in_1[6], not_234_out, not_235_out, not_236_out, in_1[2], not_237_out);
  and and_88 (and_88_out, in_1[6], not_238_out, not_239_out, not_240_out, in_1[2], not_241_out, in_1[0]);
  and and_89 (and_89_out, not_242_out, in_1[6], not_243_out, not_244_out, in_1[3], in_1[2], in_1[1]);
  and and_90 (and_90_out, in_1[6], not_245_out, not_246_out, in_1[3], in_1[2], in_1[1], in_1[0]);
  and and_91 (and_91_out, not_247_out, in_1[6], not_248_out, in_1[4], in_1[3], not_249_out, not_250_out);
  and and_92 (and_92_out, in_1[6], not_251_out, in_1[4], in_1[3], not_252_out, not_253_out, in_1[0]);
  and and_93 (and_93_out, not_254_out, in_1[6], in_1[5], not_255_out, not_256_out, not_257_out, in_1[1]);
  and and_94 (and_94_out, in_1[6], in_1[5], not_258_out, not_259_out, not_260_out, in_1[1], in_1[0]);
  and and_95 (and_95_out, not_261_out, in_1[6], in_1[5], not_262_out, in_1[3], in_1[2], not_263_out);
  and and_96 (and_96_out, in_1[6], in_1[5], not_264_out, in_1[3], in_1[2], not_265_out, in_1[0]);
  and and_97 (and_97_out, not_266_out, in_1[6], in_1[5], in_1[4], not_267_out, in_1[2], in_1[1]);
  and and_98 (and_98_out, in_1[6], in_1[5], in_1[4], not_268_out, in_1[2], in_1[1], in_1[0]);
  and and_99 (and_99_out, in_1[7], not_269_out, not_270_out, not_271_out, not_272_out, not_273_out, not_274_out, not_275_out);
  and and_100 (and_100_out, in_1[7], not_276_out, not_277_out, not_278_out, in_1[3], not_279_out, in_1[1], not_280_out);
  and and_101 (and_101_out, in_1[7], not_281_out, not_282_out, in_1[4], not_283_out, in_1[2], not_284_out, not_285_out);
  and and_102 (and_102_out, in_1[7], not_286_out, not_287_out, in_1[4], in_1[3], in_1[2], in_1[1], not_288_out);
  and and_103 (and_103_out, in_1[7], not_289_out, in_1[5], not_290_out, in_1[3], not_291_out, not_292_out, not_293_out);
  and and_104 (and_104_out, in_1[7], not_294_out, in_1[5], in_1[4], not_295_out, not_296_out, in_1[1], not_297_out);
  and and_105 (and_105_out, in_1[7], not_298_out, in_1[5], in_1[4], in_1[3], in_1[2], not_299_out, not_300_out);
  and and_106 (and_106_out, in_1[7], in_1[6], not_301_out, not_302_out, not_303_out, in_1[2], in_1[1], not_304_out);
  and and_107 (and_107_out, in_1[7], in_1[6], not_305_out, in_1[4], not_306_out, not_307_out, not_308_out, not_309_out);
  and and_108 (and_108_out, in_1[7], in_1[6], not_310_out, in_1[4], in_1[3], not_311_out, in_1[1], not_312_out);
  and and_109 (and_109_out, in_1[7], in_1[6], in_1[5], not_313_out, not_314_out, in_1[2], not_315_out, not_316_out);
  and and_110 (and_110_out, in_1[7], in_1[6], in_1[5], not_317_out, in_1[3], in_1[2], in_1[1], not_318_out);
  and and_111 (and_111_out, in_1[7], in_1[6], in_1[5], in_1[4], in_1[3], not_319_out, not_320_out, not_321_out);
  and and_112 (and_112_out, not_322_out, not_323_out, not_324_out, not_325_out, in_1[2], not_326_out);
  and and_113 (and_113_out, not_327_out, not_328_out, not_329_out, not_330_out, in_1[2], in_1[1]);
  and and_114 (and_114_out, not_331_out, not_332_out, not_333_out, in_1[3], in_1[2], in_1[1], not_334_out);
  and and_115 (and_115_out, not_335_out, not_336_out, not_337_out, in_1[4], not_338_out, not_339_out);
  and and_116 (and_116_out, not_340_out, not_341_out, not_342_out, in_1[4], in_1[3], not_343_out);
  and and_117 (and_117_out, not_344_out, not_345_out, in_1[4], in_1[3], not_346_out, not_347_out);
  and and_118 (and_118_out, not_348_out, not_349_out, in_1[4], in_1[3], not_350_out, not_351_out, not_352_out);
  and and_119 (and_119_out, not_353_out, not_354_out, in_1[5], not_355_out, not_356_out, not_357_out, in_1[1]);
  and and_120 (and_120_out, not_358_out, not_359_out, in_1[5], not_360_out, in_1[3], in_1[2]);
  and and_121 (and_121_out, not_361_out, not_362_out, in_1[5], in_1[4], not_363_out, in_1[2], in_1[1]);
  and and_122 (and_122_out, not_364_out, in_1[6], not_365_out, not_366_out, not_367_out, not_368_out);
  and and_123 (and_123_out, not_369_out, in_1[6], not_370_out, not_371_out, not_372_out, in_1[1]);
  and and_124 (and_124_out, in_1[6], not_373_out, not_374_out, in_1[3], not_375_out, in_1[1], not_376_out);
  and and_125 (and_125_out, not_377_out, in_1[6], not_378_out, not_379_out, in_1[3], in_1[2], not_380_out);
  and and_126 (and_126_out, not_381_out, in_1[6], in_1[4], not_382_out, in_1[2], not_383_out);
  and and_127 (and_127_out, in_1[6], not_384_out, in_1[4], not_385_out, in_1[2], not_386_out, not_387_out);
  and and_128 (and_128_out, not_388_out, in_1[6], not_389_out, in_1[4], in_1[2], in_1[1]);
  and and_129 (and_129_out, in_1[6], not_390_out, in_1[4], in_1[3], in_1[2], in_1[1], not_391_out);
  and and_130 (and_130_out, not_392_out, in_1[6], in_1[5], not_393_out, in_1[3], not_394_out);
  and and_131 (and_131_out, not_395_out, in_1[6], in_1[5], in_1[4], not_396_out, not_397_out, in_1[1]);
  and and_132 (and_132_out, not_398_out, in_1[6], in_1[5], in_1[4], in_1[3], in_1[2]);
  and and_133 (and_133_out, in_1[6], in_1[5], in_1[4], in_1[3], in_1[2], not_399_out, not_400_out);
  and and_134 (and_134_out, in_1[7], not_401_out, not_402_out, not_403_out, not_404_out, not_405_out, in_1[0]);
  and and_135 (and_135_out, in_1[7], not_406_out, not_407_out, not_408_out, not_409_out, not_410_out, in_1[1]);
  and and_136 (and_136_out, in_1[7], not_411_out, not_412_out, not_413_out, not_414_out, in_1[1], in_1[0]);
  and and_137 (and_137_out, in_1[7], not_415_out, not_416_out, not_417_out, in_1[2], not_418_out, not_419_out);
  and and_138 (and_138_out, in_1[7], not_420_out, not_421_out, not_422_out, in_1[3], in_1[2], not_423_out);
  and and_139 (and_139_out, in_1[7], not_424_out, not_425_out, in_1[3], in_1[2], not_426_out, not_427_out);
  and and_140 (and_140_out, in_1[7], not_428_out, in_1[4], not_429_out, in_1[2], not_430_out, in_1[0]);
  and and_141 (and_141_out, in_1[7], not_431_out, not_432_out, in_1[4], not_433_out, in_1[2], in_1[1]);
  and and_142 (and_142_out, in_1[7], not_434_out, not_435_out, in_1[4], in_1[2], in_1[1], in_1[0]);
  and and_143 (and_143_out, in_1[7], not_436_out, in_1[5], not_437_out, not_438_out, not_439_out, not_440_out);
  and and_144 (and_144_out, in_1[7], not_441_out, in_1[5], not_442_out, not_443_out, in_1[1], not_444_out);
  and and_145 (and_145_out, in_1[7], not_445_out, in_1[5], not_446_out, in_1[3], not_447_out, in_1[0]);
  and and_146 (and_146_out, in_1[7], not_448_out, in_1[5], in_1[4], not_449_out, not_450_out, in_1[1], in_1[0]);
  and and_147 (and_147_out, in_1[7], not_451_out, in_1[5], in_1[4], not_452_out, in_1[2], not_453_out);
  and and_148 (and_148_out, in_1[7], not_454_out, in_1[5], in_1[4], in_1[3], in_1[2], in_1[0]);
  and and_149 (and_149_out, in_1[7], not_455_out, in_1[5], in_1[4], in_1[3], in_1[2], in_1[1]);
  and and_150 (and_150_out, in_1[7], in_1[6], not_456_out, not_457_out, not_458_out, not_459_out, not_460_out);
  and and_151 (and_151_out, in_1[7], in_1[6], not_461_out, not_462_out, in_1[2], in_1[1], in_1[0]);
  and and_152 (and_152_out, in_1[7], in_1[6], not_463_out, not_464_out, in_1[3], not_465_out, not_466_out);
  and and_153 (and_153_out, in_1[7], in_1[6], not_467_out, in_1[3], not_468_out, not_469_out, not_470_out);
  and and_154 (and_154_out, in_1[7], in_1[6], in_1[4], not_471_out, not_472_out, not_473_out, in_1[0]);
  and and_155 (and_155_out, in_1[7], in_1[6], not_474_out, in_1[4], not_475_out, not_476_out, in_1[1]);
  and and_156 (and_156_out, in_1[7], in_1[6], not_477_out, in_1[4], not_478_out, in_1[1], in_1[0]);
  and and_157 (and_157_out, in_1[7], in_1[6], not_479_out, in_1[4], in_1[3], in_1[2], not_480_out);
  and and_158 (and_158_out, in_1[7], in_1[6], in_1[5], not_481_out, not_482_out, in_1[2], in_1[0]);
  and and_159 (and_159_out, in_1[7], in_1[6], in_1[5], not_483_out, not_484_out, in_1[2], in_1[1]);
  and and_160 (and_160_out, in_1[7], in_1[6], in_1[5], not_485_out, in_1[2], in_1[1], in_1[0]);
  and and_161 (and_161_out, in_1[7], in_1[6], in_1[5], in_1[4], not_486_out, not_487_out, not_488_out);
  and and_162 (and_162_out, in_1[7], in_1[6], in_1[5], in_1[4], in_1[3], not_489_out, in_1[0]);
  and and_163 (and_163_out, in_1[7], in_1[6], in_1[5], in_1[4], in_1[3], not_490_out, in_1[1]);
  and and_164 (and_164_out, not_491_out, not_492_out, not_493_out, not_494_out, not_495_out, in_1[1]);
  and and_165 (and_165_out, not_496_out, not_497_out, not_498_out, not_499_out, in_1[1], not_500_out);
  and and_166 (and_166_out, not_501_out, not_502_out, not_503_out, not_504_out, in_1[2], in_1[1]);
  and and_167 (and_167_out, not_505_out, not_506_out, not_507_out, in_1[2], in_1[1], not_508_out);
  and and_168 (and_168_out, not_509_out, not_510_out, not_511_out, in_1[3], in_1[2], not_512_out);
  and and_169 (and_169_out, not_513_out, not_514_out, in_1[3], in_1[2], not_515_out, not_516_out);
  and and_170 (and_170_out, not_517_out, not_518_out, not_519_out, in_1[4], not_520_out, not_521_out, not_522_out);
  and and_171 (and_171_out, not_523_out, not_524_out, in_1[4], not_525_out, not_526_out, not_527_out, not_528_out);
  and and_172 (and_172_out, not_529_out, not_530_out, not_531_out, in_1[4], in_1[3], not_532_out, in_1[1]);
  and and_173 (and_173_out, not_533_out, not_534_out, in_1[4], in_1[3], not_535_out, in_1[1], not_536_out);
  and and_174 (and_174_out, not_537_out, in_1[5], not_538_out, not_539_out, not_540_out, not_541_out);
  and and_175 (and_175_out, in_1[5], not_542_out, not_543_out, not_544_out, not_545_out, not_546_out);
  and and_176 (and_176_out, not_547_out, not_548_out, in_1[5], not_549_out, in_1[2], not_550_out);
  and and_177 (and_177_out, not_551_out, in_1[5], not_552_out, in_1[2], not_553_out, not_554_out);
  and and_178 (and_178_out, not_555_out, in_1[5], not_556_out, in_1[3], not_557_out, in_1[1]);
  and and_179 (and_179_out, in_1[5], not_558_out, in_1[3], not_559_out, in_1[1], not_560_out);
  and and_180 (and_180_out, not_561_out, not_562_out, in_1[5], in_1[3], in_1[2], in_1[1]);
  and and_181 (and_181_out, not_563_out, in_1[5], in_1[3], in_1[2], in_1[1], not_564_out);
  and and_182 (and_182_out, not_565_out, not_566_out, in_1[5], in_1[4], in_1[3], not_567_out, not_568_out);
  and and_183 (and_183_out, not_569_out, in_1[5], in_1[4], in_1[3], not_570_out, not_571_out, not_572_out);
  and and_184 (and_184_out, not_573_out, in_1[6], not_574_out, not_575_out, in_1[3], not_576_out);
  and and_185 (and_185_out, in_1[6], not_577_out, not_578_out, in_1[3], not_579_out, not_580_out);
  and and_186 (and_186_out, not_581_out, in_1[6], not_582_out, in_1[3], in_1[2], not_583_out);
  and and_187 (and_187_out, in_1[6], not_584_out, in_1[3], in_1[2], not_585_out, not_586_out);
  and and_188 (and_188_out, not_587_out, in_1[6], not_588_out, in_1[4], not_589_out, in_1[1]);
  and and_189 (and_189_out, in_1[6], not_590_out, in_1[4], not_591_out, in_1[1], not_592_out);
  and and_190 (and_190_out, not_593_out, in_1[6], in_1[5], not_594_out, not_595_out, in_1[2], in_1[1]);
  and and_191 (and_191_out, in_1[6], in_1[5], not_596_out, not_597_out, in_1[2], in_1[1], not_598_out);
  and and_192 (and_192_out, not_599_out, in_1[6], in_1[5], in_1[4], not_600_out, not_601_out);
  and and_193 (and_193_out, in_1[6], in_1[5], in_1[4], not_602_out, not_603_out, not_604_out);
  and and_194 (and_194_out, not_605_out, in_1[6], in_1[5], in_1[4], in_1[3], in_1[1]);
  and and_195 (and_195_out, in_1[6], in_1[5], in_1[4], in_1[3], in_1[1], not_606_out);
  and and_196 (and_196_out, in_1[7], not_607_out, not_608_out, not_609_out, not_610_out, not_611_out, in_1[0]);
  and and_197 (and_197_out, in_1[7], not_612_out, not_613_out, not_614_out, in_1[2], not_615_out, in_1[0]);
  and and_198 (and_198_out, in_1[7], not_616_out, not_617_out, in_1[3], not_618_out, in_1[1], in_1[0]);
  and and_199 (and_199_out, in_1[7], not_619_out, not_620_out, in_1[3], in_1[2], in_1[1], in_1[0]);
  and and_200 (and_200_out, in_1[7], not_621_out, not_622_out, in_1[4], in_1[3], not_623_out, not_624_out, in_1[0]);
  and and_201 (and_201_out, in_1[7], not_625_out, in_1[5], not_626_out, not_627_out, in_1[1], in_1[0]);
  and and_202 (and_202_out, in_1[7], in_1[5], not_628_out, in_1[3], not_629_out, not_630_out, in_1[0]);
  and and_203 (and_203_out, in_1[7], not_631_out, in_1[5], in_1[3], in_1[2], not_632_out, in_1[0]);
  and and_204 (and_204_out, in_1[7], not_633_out, in_1[5], in_1[4], not_634_out, in_1[1], in_1[0]);
  and and_205 (and_205_out, in_1[7], in_1[5], in_1[4], not_635_out, not_636_out, in_1[1], in_1[0]);
  and and_206 (and_206_out, in_1[7], in_1[6], not_637_out, not_638_out, not_639_out, in_1[2], in_1[1], in_1[0]);
  and and_207 (and_207_out, in_1[7], in_1[6], not_640_out, in_1[4], not_641_out, not_642_out, in_1[0]);
  and and_208 (and_208_out, in_1[7], in_1[6], not_643_out, in_1[4], in_1[3], in_1[1], in_1[0]);
  and and_209 (and_209_out, in_1[7], in_1[6], in_1[5], not_644_out, not_645_out, in_1[2], not_646_out, in_1[0]);
  and and_210 (and_210_out, in_1[7], in_1[6], in_1[5], not_647_out, in_1[3], in_1[2], in_1[1], in_1[0]);
  and and_211 (and_211_out, in_1[7], in_1[6], in_1[5], in_1[4], in_1[3], not_648_out, in_1[0]);
  or or_1 (out_3[0], and_1_out, and_2_out, and_3_out, and_4_out, and_5_out, and_6_out, and_7_out);
  or or_2 (out_4[3], and_8_out, and_9_out, and_10_out, and_11_out, and_12_out, and_13_out);
  or or_3 (out_4[2], and_14_out, and_15_out, and_16_out, and_17_out, and_18_out, and_19_out, and_20_out, and_21_out, and_22_out);
  or or_4 (out_4[1], and_23_out, and_24_out, and_25_out, and_26_out, and_27_out, and_28_out, and_29_out, and_30_out, and_31_out, and_32_out, and_33_out, and_34_out, and_35_out, and_36_out, and_37_out, and_38_out, and_39_out, and_40_out, and_41_out, and_42_out);
  or or_5 (or_5_out, and_75_out, and_76_out, and_77_out, and_78_out, and_79_out, and_80_out, and_81_out, and_82_out, and_83_out, and_84_out, and_85_out, and_86_out, and_87_out, and_88_out, and_89_out, and_90_out, and_91_out, and_92_out, and_93_out);
  or or_6 (or_6_out, and_94_out, and_95_out, and_96_out, and_97_out, and_98_out, and_99_out, and_100_out, and_101_out, and_102_out, and_103_out, and_104_out, and_105_out, and_106_out, and_107_out, and_108_out, and_109_out, and_110_out, and_111_out);
  or or_7 (or_7_out, and_164_out, and_165_out, and_166_out, and_167_out, and_168_out, and_169_out, and_170_out, and_171_out, and_172_out, and_173_out, and_174_out, and_175_out, and_176_out, and_177_out, and_178_out, and_179_out, and_180_out, and_181_out, and_182_out, and_183_out, and_184_out, and_185_out, and_186_out, and_187_out);
  or or_8 (or_8_out, and_188_out, and_189_out, and_190_out, and_191_out, and_192_out, and_193_out, and_194_out, and_195_out, and_196_out, and_197_out, and_198_out, and_199_out, and_200_out, and_201_out, and_202_out, and_203_out, and_204_out, and_205_out, and_206_out, and_207_out, and_208_out, and_209_out, and_210_out, and_211_out);
  or or_9 (out_4[0], and_43_out, and_44_out, and_45_out, and_46_out, and_47_out, and_48_out, and_49_out, and_50_out, and_51_out, and_52_out, and_53_out, and_54_out, and_55_out, and_56_out, and_57_out, and_58_out, and_59_out, and_60_out, and_61_out, and_62_out, and_63_out, and_64_out, and_65_out, and_66_out, and_67_out, and_68_out, and_69_out, and_70_out, and_71_out, and_72_out, and_73_out, and_74_out);
  or or_10 (out_5[3], or_5_out, or_6_out);
  or or_11 (or_11_out, and_112_out, and_113_out, and_114_out, and_115_out, and_116_out, and_117_out, and_118_out, and_119_out, and_120_out, and_121_out, and_122_out, and_123_out, and_124_out, and_125_out, and_126_out, and_127_out, and_128_out, and_129_out, and_130_out, and_131_out, and_132_out, and_133_out, and_134_out, and_135_out, and_136_out, and_137_out);
  or or_12 (out_5[2], or_11_out, or_13_out);
  or or_13 (or_13_out, and_138_out, and_139_out, and_140_out, and_141_out, and_142_out, and_143_out, and_144_out, and_145_out, and_146_out, and_147_out, and_148_out, and_149_out, and_150_out, and_151_out, and_152_out, and_153_out, and_154_out, and_155_out, and_156_out, and_157_out, and_158_out, and_159_out, and_160_out, and_161_out, and_162_out, and_163_out);
  or or_14 (out_5[1], or_7_out, or_8_out);

  assign F1 = in_1[7];
  assign out_3[3:1] = 3'b000;
  assign out_5[0] = in_1[0];
endmodule

module \Circuito_Botão  (
  input  Q3,
  input  Q2,
  input  Q1,
  input  Q0,
  output T3,
  output T2,
  output T1,
  output T0
);

  wire and_1_out, and_2_out, and_3_out, and_4_out, and_5_out, and_6_out, and_7_out, and_8_out, not_1_out,
       not_2_out, not_3_out, not_4_out, not_5_out, not_6_out, not_7_out, not_8_out, not_9_out, not_10_out,
       not_11_out;

  or or_1 (T3, Q2, Q3);
  and and_1 (and_1_out, Q1, not_1_out);
  not not_1 (not_1_out, Q0);
  and and_2 (and_2_out, Q3, Q1);
  not not_2 (not_2_out, Q1);
  not not_3 (not_3_out, Q3);
  not not_4 (not_4_out, Q2);
  not not_5 (not_5_out, Q0);
  not not_6 (not_6_out, Q3);
  not not_7 (not_7_out, Q2);
  and and_3 (and_3_out, not_6_out, not_7_out, not_8_out);
  not not_8 (not_8_out, Q1);
  not not_9 (not_9_out, Q2);
  not not_10 (not_10_out, Q1);
  and and_4 (and_4_out, not_9_out, not_10_out, not_11_out);
  not not_11 (not_11_out, Q0);
  or or_2 (T2, and_1_out, Q2, and_2_out);
  and and_5 (and_5_out, not_2_out, Q0);
  and and_6 (and_6_out, not_3_out, not_4_out, Q1, not_5_out);
  and and_7 (and_7_out, Q2, Q0);
  and and_8 (and_8_out, Q3, Q0);
  or or_3 (T0, and_3_out, and_4_out);
  or or_4 (T1, and_5_out, and_6_out, and_7_out, and_8_out);
endmodule

module \Botão  (
  input  in_1,
  output [3:0] out_2
);

  wire \circuito_botão_1_t0 , \circuito_botão_1_t1 , \circuito_botão_1_t2 , \circuito_botão_1_t3 ;

  T_Flip_Flop t_ff_1 (.clk(in_1), .T(\circuito_botão_1_t0 ), .Q(out_2[0]));  // open: Qn, preset, reset, en
  T_Flip_Flop t_ff_2 (.clk(in_1), .T(\circuito_botão_1_t1 ), .Q(out_2[1]));  // open: Qn, preset, reset, en
  T_Flip_Flop t_ff_3 (.clk(in_1), .T(\circuito_botão_1_t2 ), .Q(out_2[2]));  // open: Qn, preset, reset, en
  \Circuito_Botão  \circuito_botão_1  (
    .Q3(out_2[3]), .Q2(out_2[2]), .Q1(out_2[1]), .Q0(out_2[0]), .T3(\circuito_botão_1_t3 ),
    .T2(\circuito_botão_1_t2 ), .T1(\circuito_botão_1_t1 ), .T0(\circuito_botão_1_t0 ));
  T_Flip_Flop t_ff_4 (.clk(in_1), .T(\circuito_botão_1_t3 ), .Q(out_2[3]));  // open: Qn, preset, reset, en

  // Notes on the sheet:
  //   Circuito Combinacional
endmodule
