// Logisim project Somador.circ as structural Verilog: 3 circuits, main circuit main
module main (
  input  in_1,
  input  in_2,
  input  in_3,
  input  in_4,
  input  in_5,
  input  in_6,
  output out_7
);

  wire decodificador_1_a, decodificador_1_b, decodificador_1_c, decodificador_1_d, decodificador_1_e,
       decodificador_1_f, decodificador_1_g, somador_1_s0, somador_1_s1, somador_1_s2;

  Somador somador_1 (
    .Q2(in_1), .Q1(in_2), .Q0(in_3), .Q1_2(in_4), .Q2_2(in_5), .Q0_2(in_6), .S2(somador_1_s2),
    .S1(somador_1_s1), .S0(somador_1_s0), .Overflow(out_7));
  Decodificador decodificador_1 (
    .Q0(somador_1_s2), .Q1(somador_1_s1), .Q2(somador_1_s0), .a(decodificador_1_a), .b(decodificador_1_b),
    .c(decodificador_1_c), .d(decodificador_1_d), .e(decodificador_1_e), .f(decodificador_1_f),
    .g(decodificador_1_g));
  _7_Segment_Display u_7_segment_display_1 (
    .g(decodificador_1_g), .f(decodificador_1_f), .a(decodificador_1_a), .b(decodificador_1_b),
    .e(decodificador_1_e), .d(decodificador_1_d), .c(decodificador_1_c));  // open: dp
endmodule

module Decodificador (
  input  Q0,
  input  Q1,
  input  Q2,
  output a,
  output b,
  output c,
  output d,
  output e,
  output f,
  output g
);

  wire and_1_out, and_2_out, and_3_out, and_4_out, and_5_out, and_6_out, and_7_out, and_8_out, and_9_out,
       and_10_out, and_11_out, and_12_out, and_13_out, and_14_out, and_15_out, and_16_out, not_1_out,
       not_2_out, not_3_out, not_4_out, not_5_out, not_6_out, not_7_out, not_8_out, not_9_out, not_10_out,
       not_11_out, not_12_out, not_13_out, not_14_out, not_15_out, not_16_out, not_17_out, not_18_out,
       not_19_out, not_20_out, not_21_out;

  not not_1 (not_1_out, Q0);
  not not_2 (not_2_out, Q2);
  not not_3 (not_3_out, Q1);
  not not_4 (not_4_out, Q2);
  not not_5 (not_5_out, Q1);
  not not_6 (not_6_out, Q0);
  not not_7 (not_7_out, Q2);
  not not_8 (not_8_out, Q0);
  not not_9 (not_9_out, Q2);
  not not_10 (not_10_out, Q1);
  not not_11 (not_11_out, Q0);
  not not_12 (not_12_out, Q2);
  not not_13 (not_13_out, Q2);
  not not_14 (not_14_out, Q1);
  not not_15 (not_15_out, Q2);
  not not_16 (not_16_out, Q1);
  not not_17 (not_17_out, Q2);
  not not_18 (not_18_out, Q0);
  not not_19 (not_19_out, Q1);
  not not_20 (not_20_out, Q2);
  and and_1 (and_1_out, not_1_out, not_2_out);
  and and_2 (and_2_out, Q0, Q2);
  not not_21 (not_21_out, Q0);
  and and_3 (and_3_out, not_3_out, not_4_out);
  and and_4 (and_4_out, Q1, Q2);
  or or_1 (c, not_5_out, Q2, Q0);
  and and_5 (and_5_out, not_6_out, not_7_out);
  and and_6 (and_6_out, not_8_out, Q1);
  and and_7 (and_7_out, Q1, not_9_out);
  and and_8 (and_8_out, Q0, not_10_out, Q2);
  and and_9 (and_9_out, not_11_out, not_12_out);
  and and_10 (and_10_out, Q1, not_13_out);
  and and_11 (and_11_out, not_14_out, not_15_out);
  and and_12 (and_12_out, Q0, not_16_out);
  and and_13 (and_13_out, Q0, not_17_out);
  and and_14 (and_14_out, not_18_out, Q1);
  and and_15 (and_15_out, Q0, not_19_out);
  and and_16 (and_16_out, Q0, not_20_out);
  or or_2 (a, and_1_out, Q1, and_2_out);
  or or_3 (b, not_21_out, and_3_out, and_4_out);
  or or_4 (d, and_5_out, and_6_out, and_7_out, and_8_out);
  or or_5 (e, and_9_out, and_10_out);
  or or_6 (f, and_11_out, and_12_out, and_13_out);
  or or_7 (g, and_14_out, and_15_out, and_16_out);
endmodule

module Somador (
  input  Q2,
  input  Q1,
  input  Q0,
  input  Q1_2,
  input  Q2_2,
  input  Q0_2,
  output S2,
  output S1,
  output S0,
  output Overflow
);

  wire adder_1_cout, adder_2_cout;

  Adder #(.width(1)) adder_1 (.a(Q0), .b(Q0_2), .out(S0), .cin(1'b0), .cout(adder_1_cout));
  Adder #(.width(1)) adder_2 (.a(Q1), .b(Q2_2), .out(S1), .cin(adder_1_cout), .cout(adder_2_cout));
  Adder #(.width(1)) adder_3 (.a(Q2), .b(Q1_2), .out(S2), .cin(adder_2_cout), .cout(Overflow));
endmodule
