# Fritzing sketch Simulação do Contador - Fritzing (saved by Fritzing 0.7.11b)
breadboards: 1

parts:
  Arduino1 = Arduino
  7_Segment1 = 7 Segment Display
  S1 = Pushbutton [package="[THT]"]
  R1 = Resistor [tolerance=±5% resistance=330 package=THT]
  R2 = Resistor [tolerance=±5% resistance=330 package=THT]
  R3 = Resistor [tolerance=±5% resistance=330 package=THT]
  R4 = Resistor [tolerance=±5% resistance=330 package=THT]
  R6 = Resistor [tolerance=±5% resistance=330 package=THT]
  R7 = Resistor [tolerance=±5% resistance=330 package=THT]
  R8 = Resistor [tolerance=±5% resistance=330 package=THT]
  R9 = Resistor [tolerance=±5% resistance=330 package=THT]
  R10 = Resistor [tolerance=±5% resistance=330 package=THT]

nets:
  N1: Arduino1.D13, S1.Pin_1, S1.Pin_2, R1.Pin_0
  N2: Arduino1.D9, R6.Pin_0
  N3: Arduino1.D8, R8.Pin_0
  N4: Arduino1.D7, R3.Pin_1
  N5: Arduino1.D6, R4.Pin_1
  N6: Arduino1.D5, R10.Pin_0
  N7: Arduino1.D4, R7.Pin_0
  N8: Arduino1.D3, R9.Pin_0
  N9: Arduino1.D2, R2.Pin_1
  N10: Arduino1.+5V, S1.Pin_3, S1.Pin_4
  N11: Arduino1.GND, 7_Segment1.common_cathode#3, 7_Segment1.Segment_E, R1.Pin_1, R3.Pin_0
  N12: 7_Segment1.Segment_F, R2.Pin_0
  N13: 7_Segment1.Segment_D, R4.Pin_0
  N14: 7_Segment1.Segment_DP, R10.Pin_1
  N15: 7_Segment1.Segment_C, R6.Pin_1
  N16: 7_Segment1.common_cathode#8, R7.Pin_1
  N17: 7_Segment1.Segment_B, R8.Pin_1
  N18: 7_Segment1.Segment_A#10, R9.Pin_1
